// Logisim project cpu_benchmark.circ as structural Verilog: 4 circuits, main circuit cpu
module cpu (
);

  wire _5ExtImm, and_1_out, and_3_out, clk, comparator_1_eq, controler_1__16extimm, controler_1_regwrite,
       controler_1_sextimm, controler_1_sh, controler_1_sw, ERET, GO, IR1, IR2, IR3, mips_ram_1_p3,
       not_1_out, or_2_out, RST, syscall, W1, W2, W3;
  wire [0:0] and_2_out, controler_1_lw;
  wire [1:0] mips_ram_1_p5, or_1_out, or_3_out;
  wire [3:0] controler_1_aluop;
  wire [4:0] multiplexer_3_out, rA_t, rB_t, Rs, Rt;
  wire [15:0] counter_1_q, load_use, \总周期数 , \插入气泡数 , \无条件分支指令数 , \有条件分支成功跳转 , \有条件分支指令数 ;
  wire [31:0] adder_2_out, alu_1_result, bit_extender_1_out, bit_extender_2_out, cpo_regs_1_pc_2,
       mips_ram_1_p7, multiplexer_4_out, multiplexer_5_out, multiplexer_6_out, multiplexer_7_out,
       npc_1_nextpc, PC_q, RA, RB, rom_1_data, SyscallOut;

  Button \u_总复位  (.out(RST));
  Button _1 (.out(IR1));
  Button _2 (.out(IR2));
  Button _3 (.out(IR3));
  Button u_GO (.out(GO));
  LED led_1 (.in(W1));
  LED led_2 (.in(W2));
  LED led_3 (.in(W3));
  Clock clock_1 (.out(clk));
  Hex_Digit_Display hex_digit_display_1 (.value(SyscallOut[31:28]));  // open: dp
  Comparator #(.width(32)) comparator_1 (.a(RA), .b(32'h22), .eq(comparator_1_eq));  // open: gt, lt
  Hex_Digit_Display hex_digit_display_2 (.value(SyscallOut[23:20]));  // open: dp
  Hex_Digit_Display hex_digit_display_3 (.value(SyscallOut[27:24]));  // open: dp
  NPC npc_1 (
    .Reset(RST), .CLK(clk), .IM({rom_1_data[31:26], Rs, Rt, rom_1_data[15:0]}), .PC(PC_q), .RegRS(RA),
    .RegRT(RB), .OFFSET(multiplexer_5_out), .NextPC(npc_1_nextpc), .unconditional(\无条件分支指令数 ),
    .conditional(\有条件分支指令数 ), .conditionalsucces(\有条件分支成功跳转 ));
  and and_1 (and_1_out, ~GO, ~comparator_1_eq);  // AND_Gate
  Multiplexer #(.width(5), .enable("false")) multiplexer_1 (.in0(Rs), .in1(5'b00010), .out(rA_t), .sel(syscall));
  Hex_Digit_Display hex_digit_display_4 (.value(SyscallOut[15:12]));  // open: dp
  Hex_Digit_Display hex_digit_display_5 (.value(SyscallOut[19:16]));  // open: dp
  and and_2 (and_2_out[0], and_1_out, syscall);
  Hex_Digit_Display hex_digit_display_6 (.value(SyscallOut[7:4]));  // open: dp
  Hex_Digit_Display hex_digit_display_7 (.value(SyscallOut[11:8]));  // open: dp
  CPO_regs cpo_regs_1 (
    .PC(npc_1_nextpc), .CLK(clk), .IR1(IR1), .W1(W1), .ERET(ERET), .IR2(IR2), .W2(W2), .IR3(IR3), .W3(W3),
    .pc_2(cpo_regs_1_pc_2), .RST(RST));
  not not_1 (not_1_out, and_2_out[0]);
  Multiplexer #(.width(5), .enable("false")) multiplexer_2 (.in0(Rt), .in1(5'b00100), .out(rB_t), .sel(syscall));
  Hex_Digit_Display hex_digit_display_8 (.value(SyscallOut[3:0]));  // open: dp
  Register #(.width(32)) PC (.D(cpo_regs_1_pc_2), .en(not_1_out), .Q(PC_q), .clk(clk), .clr(RST));
  Counter #(.width(16), .max('hffff)) counter_1 (
    .count(not_1_out), .Q(counter_1_q), .clk(clk), .clr(RST));  // open: load, D, carry
  Adder #(.width(16)) adder_1 (.a(counter_1_q), .b({{15{1'b0}}, and_2_out[0]}), .out(\总周期数 ));  // open: cin, cout
  // Probe on \总周期数 
  // Probe on \无条件分支指令数 
  // Probe on load_use
  // Probe on \有条件分支成功跳转 
  // Probe on \插入气泡数 
  ROM #(.addrWidth(10), .dataWidth(32)) rom_1 (
    .addr(PC_q[11:2]), .data({rom_1_data[31:26], Rs, Rt, rom_1_data[15:0]}));  // open: sel
  assign bit_extender_1_out = {{16{rom_1_data[15]}}, rom_1_data[15:0]};  // Bit_Extender bit_extender_1
  assign bit_extender_2_out = {{27{1'b0}}, rom_1_data[10:6]};  // Bit_Extender bit_extender_2
  Adder #(.width(32)) adder_2 (.a(32'h4), .b(PC_q), .out(adder_2_out));  // open: cin, cout
  Multiplexer #(.select(2), .width(5), .enable("false")) multiplexer_3 (
    .in0(rom_1_data[15:11]), .in1(Rt), .in2({5{1'b1}}), .out(multiplexer_3_out), .sel(or_1_out));  // open: in3
  or or_1 (or_1_out[0], controler_1__16extimm, controler_1_sextimm);
  controler controler_1 (
    .operator(rom_1_data[31:26]), .func(rom_1_data[5:0]), .AluOp(controler_1_aluop), .LW(controler_1_lw[0]),
    ._16ExtImm(controler_1__16extimm), .JAL(or_1_out[1]), .syscall(syscall), .SW(controler_1_sw),
    .SExtImm(controler_1_sextimm), ._5ExtImm(_5ExtImm), .SH(controler_1_sh), .RegWrite(controler_1_regwrite),
    .enchange(or_3_out[1]), .ERET(ERET));
  and and_3 (and_3_out, syscall, ~and_2_out[0]);  // AND_Gate
  Multiplexer #(.select(2), .width(32), .enable("false")) multiplexer_4 (
    .in0(alu_1_result), .in1(mips_ram_1_p7), .in2(adder_2_out), .out(multiplexer_4_out),
    .sel({or_1_out[1], controler_1_lw[0]}));  // open: in3
  Register #(.width(32)) a0 (.D(RB), .en(and_3_out), .Q(SyscallOut), .clk(clk), .clr(RST));
  Multiplexer #(.width(32), .enable("false")) multiplexer_5 (
    .in0(bit_extender_1_out), .in1(bit_extender_2_out), .out(multiplexer_5_out), .sel(_5ExtImm));
  // RegisterFile registerfile_1: pin names not known; wires that end beside it: multiplexer_4_out, clk, controler_1_regwrite, multiplexer_3_out, rA_t, rB_t, RA, RB
  or or_2 (or_2_out, _5ExtImm, or_3_out[1]);
  Multiplexer #(.width(32), .enable("false")) multiplexer_6 (
    .in0(RA), .in1(RB), .out(multiplexer_6_out), .sel(or_2_out));
  Multiplexer #(.select(2), .width(32), .enable("false")) multiplexer_7 (
    .in0(RB), .in1(multiplexer_5_out), .in2(RA), .out(multiplexer_7_out), .sel(or_3_out));  // open: in3
  or or_3 (or_3_out[0], controler_1__16extimm, controler_1_sextimm, _5ExtImm);
  ALU alu_1 (
    .AluOP(controler_1_aluop), .X(multiplexer_6_out), .Result(alu_1_result), .Y(multiplexer_7_out));  // open: Equal, Signed_Overflow, Result_2, UnSigned_Overflow
  // MIPS_RAM mips_ram_1: pin names not known; wires that end beside it: alu_1_result[11:0], RB, mips_ram_1_p3, clk, mips_ram_1_p5, RST, mips_ram_1_p7
  or or_4 (mips_ram_1_p3, controler_1_sw, controler_1_sh);
  Multiplexer #(.width(2), .enable("false")) multiplexer_8 (
    .in0(2'b00), .in1(2'b10), .out(mips_ram_1_p5), .sel(controler_1_sh));

  // Notes on the sheet:
  //   数码管输出应该用寄存器锁存，否则显示数据只能一闪而过
  //   可以通过项目增加Logisim库的方式将前几次实验完成的电路作为子电路引入到本电路中使用
  //   数码管输出
  //   总复位信号应将除ROM以外所有存储组件全部清零
  //   指令存储器
  //   contents of rom_1 (hex, n*v repeats v):
  //   201d00ff 20110200 20020022 112020 c 2231ffff 1620fffc 20020032 c 20080001 20090003 20110876 112020
  //   20020022 c 200b0008 1118804 1318804 112020 20020022 c 216bffff 1560fff9 20020032 c 20080001 20090003
  //   20110876 118d00 112020 20020022 c 200b0008 1118806 1318806 112020 20020022 c 216bffff 1560fff9
  //   20020032 c 20090000 200b0020 20110001 20120001 a5310000 112020 20020022 c 2328820 21290002 216bffff
  //   1560fff8 200b0010 20090000 8d310000 112020 20020022 c 21290004 216bffff 1560fff9 20020032 c 2011000f
  //   112020 20020022 c 2231ffff 1e20fffb 20020032 c 2002000a c 2001001c 3a1e822 afb60000 afb40004
  //   afb50008 afb3000c afb00010 afa40014 afa20018 20160001 20140006 20150001 168020 108100 2149825 132020
  //   20020022 c 1600fffa 295a022 1680fff7 8fb60000 8fb40004 8fb50008 8fb3000c 8fb00010 8fa40014 8fa20018
  //   23bd001c 42000018 2001001c 3a1e822 afb60000 afb40004 afb50008 afb3000c afb00010 afa40014 afa20018
  //   20160002 20140006 20150001 168020 108100 2149825 132020 20020022 c 1600fffa 295a022 1680fff7
  //   8fb60000 8fb40004 8fb50008 8fb3000c 8fb00010 8fa40014 8fa20018 23bd001c 42000018 2001001c 3a1e822
  //   afb60000 afb40004 afb50008 afb3000c afb00010 afa40014 afa20018 20160003 20140006 20150001 168020
  //   108100 2149825 132020 20020022 c 1600fffa 295a022 1680fff7 8fb60000 8fb40004 8fb50008 8fb3000c
  //   8fb00010 8fa40014 8fa20018 23bd001c 42000018
  //   AluOp
  //   寄存器文件
endmodule

module controler (
  input  [5:0] operator,
  input  [5:0] func,
  output syscall,
  output _16ExtImm,
  output SExtImm,
  output _5ExtImm,
  output [3:0] AluOp,
  output LW,
  output SW,
  output SH,
  output RegWrite,
  output enchange,
  output JAL,
  output ERET
);

  wire ADD, ADDI, ADDIU, ADDU, AND, ANDI, BEQ, BGTZ, BNE, comparator_2_eq, comparator_3_eq, comparator_6_eq,
       comparator_8_eq, comparator_9_eq, comparator_10_eq, comparator_11_eq, comparator_12_eq,
       comparator_13_eq, comparator_15_eq, comparator_16_eq, comparator_17_eq, comparator_19_eq,
       comparator_27_eq, comparator_28_eq, comparator_29_eq, comparator_30_eq, JR, NOR, OR, ORI, R1, SLL,
       SLLV, SLT, SLTI, SLTU, SRA, SRL, SRLV, SUB;
  wire [3:0] and_16_out, and_17_out, and_18_out, and_19_out, and_20_out, and_21_out, and_22_out, and_23_out,
       and_24_out, and_25_out;
  wire [3:3] or_1_out, or_2_out, or_3_out, or_4_out, or_5_out, or_6_out;

  Comparator #(.width(6)) comparator_1 (.a(operator), .b({6{1'b0}}), .eq(R1));  // open: gt, lt
  Comparator #(.width(6)) comparator_2 (.a(func), .b(6'b100000), .eq(comparator_2_eq));  // open: gt, lt
  Comparator #(.width(6)) comparator_3 (.a(func), .b(6'b100001), .eq(comparator_3_eq));  // open: gt, lt
  Comparator #(.width(6)) comparator_4 (.a(operator), .b(6'b001000), .eq(ADDI));  // open: gt, lt
  Comparator #(.width(6)) comparator_5 (.a(operator), .b(6'b001001), .eq(ADDIU));  // open: gt, lt
  Comparator #(.width(6)) comparator_6 (.a(func), .b(6'b100100), .eq(comparator_6_eq));  // open: gt, lt
  Comparator #(.width(6)) comparator_7 (.a(operator), .b(6'b001100), .eq(ANDI));  // open: gt, lt
  Comparator #(.width(6)) comparator_8 (.a(func), .b({6{1'b0}}), .eq(comparator_8_eq));  // open: gt, lt
  Comparator #(.width(6)) comparator_9 (.a(func), .b(6'b000100), .eq(comparator_9_eq));  // open: gt, lt
  Comparator #(.width(6)) comparator_10 (.a(func), .b(6'b000010), .eq(comparator_10_eq));  // open: gt, lt
  Comparator #(.width(6)) comparator_11 (.a(func), .b(6'b000110), .eq(comparator_11_eq));  // open: gt, lt
  Comparator #(.width(6)) comparator_12 (.a(func), .b(6'b000011), .eq(comparator_12_eq));  // open: gt, lt
  Comparator #(.width(6)) comparator_13 (.a(func), .b(6'b100101), .eq(comparator_13_eq));  // open: gt, lt
  Comparator #(.width(6)) comparator_14 (.a(operator), .b(6'b001101), .eq(ORI));  // open: gt, lt
  Comparator #(.width(6)) comparator_15 (.a(func), .b(6'b100111), .eq(comparator_15_eq));  // open: gt, lt
  Comparator #(.width(6)) comparator_16 (.a(func), .b(6'b101010), .eq(comparator_16_eq));  // open: gt, lt
  Comparator #(.width(6)) comparator_17 (.a(func), .b(6'b101011), .eq(comparator_17_eq));  // open: gt, lt
  Comparator #(.width(6)) comparator_18 (.a(operator), .b(6'b001010), .eq(SLTI));  // open: gt, lt
  Comparator #(.width(6)) comparator_19 (.a(func), .b(6'b100010), .eq(comparator_19_eq));  // open: gt, lt
  Comparator #(.width(6)) comparator_20 (.a(operator), .b(6'b000101), .eq(BNE));  // open: gt, lt
  Comparator #(.width(6)) comparator_21 (.a(operator), .b(6'b000111), .eq(BGTZ));  // open: gt, lt
  Comparator #(.width(6)) comparator_22 (.a(operator), .b(6'b000100), .eq(BEQ));  // open: gt, lt
  Comparator #(.width(6)) comparator_23 (.a(operator), .b(6'b100011), .eq(LW));  // open: gt, lt
  Comparator #(.width(6)) comparator_24 (.a(operator), .b(6'b101011), .eq(SW));  // open: gt, lt
  Comparator #(.width(6)) comparator_25 (.a(operator), .b(6'b101001), .eq(SH));  // open: gt, lt
  and and_1 (ADD, R1, comparator_2_eq);
  and and_2 (ADDU, R1, comparator_3_eq);
  and and_3 (AND, R1, comparator_6_eq);
  and and_4 (SLL, R1, comparator_8_eq);
  and and_5 (SLLV, R1, comparator_9_eq);
  and and_6 (SRL, R1, comparator_10_eq);
  and and_7 (SRLV, R1, comparator_11_eq);
  and and_8 (SRA, R1, comparator_12_eq);
  and and_9 (OR, R1, comparator_13_eq);
  and and_10 (NOR, R1, comparator_15_eq);
  and and_11 (SLT, R1, comparator_16_eq);
  and and_12 (SLTU, R1, comparator_17_eq);
  and and_13 (SUB, R1, comparator_19_eq);
  Comparator #(.width(6)) comparator_26 (.a(operator), .b(6'b000011), .eq(JAL));  // open: gt, lt
  Comparator #(.width(6)) comparator_27 (.a(func), .b(6'b001000), .eq(comparator_27_eq));  // open: gt, lt
  Comparator #(.width(6)) comparator_28 (.a(func), .b(6'b001100), .eq(comparator_28_eq));  // open: gt, lt
  and and_14 (JR, R1, comparator_27_eq);
  and and_15 (syscall, R1, comparator_28_eq);
  or or_1 (or_1_out[3], ADD, ADDI, ADDU, ADDIU, SW, LW, SH);
  or or_2 (or_2_out[3], AND, ANDI);
  or or_3 (or_3_out[3], OR, ORI);
  or or_4 (or_4_out[3], SLL, SLLV);
  or or_5 (or_5_out[3], SLT, SLTI);
  or or_6 (or_6_out[3], SRL, SRLV);
  assign and_16_out = 4'b0101 & {4{or_1_out[3]}};  // AND_Gate and_16, 4 bits wide
  assign and_17_out = 4'b0111 & {4{or_2_out[3]}};  // AND_Gate and_17, 4 bits wide
  assign and_18_out = 4'b1000 & {4{or_3_out[3]}};  // AND_Gate and_18, 4 bits wide
  assign and_19_out = 4'b0000 & {4{or_4_out[3]}};  // AND_Gate and_19, 4 bits wide
  assign and_20_out = 4'b1010 & {4{NOR}};  // AND_Gate and_20, 4 bits wide
  assign and_21_out = 4'b0001 & {4{SRA}};  // AND_Gate and_21, 4 bits wide
  assign and_22_out = 4'b1011 & {4{or_5_out[3]}};  // AND_Gate and_22, 4 bits wide
  assign and_23_out = 4'b1100 & {4{SLTU}};  // AND_Gate and_23, 4 bits wide
  assign and_24_out = 4'b0110 & {4{SUB}};  // AND_Gate and_24, 4 bits wide
  assign and_25_out = 4'b0010 & {4{or_6_out[3]}};  // AND_Gate and_25, 4 bits wide
  Comparator #(.width(6)) comparator_29 (.a(operator), .b(6'b010000), .eq(comparator_29_eq));  // open: gt, lt
  Comparator #(.width(6)) comparator_30 (.a(func), .b(6'b011000), .eq(comparator_30_eq));  // open: gt, lt
  assign AluOp = and_16_out | and_17_out | and_18_out | and_19_out | and_20_out | and_21_out | and_22_out | and_23_out | and_24_out | and_25_out;  // OR_Gate or_7, 4 bits wide
  and and_26 (ERET, comparator_29_eq, comparator_30_eq);
  or or_8 (_16ExtImm, ANDI, ORI);
  or or_9 (SExtImm, ADDI, ADDIU, LW, SW, SH, BNE, BGTZ, BEQ, SLTI);
  or or_10 (_5ExtImm, SLL, SRA, SRL);
  or or_11 (enchange, SRLV, SLLV);
  or or_12 (RegWrite, SRLV, ADD, ADDU, ADDI, ADDIU, AND, ANDI, SLL, SLLV, SRL, SRA, OR, ORI, NOR, SLT, SLTU, SLTI, SUB, JAL, LW);

  // Other names for the same wires on the sheet: operate[5:0] = operator; sllv_srlv = enchange
endmodule

module NPC (
  input  Reset,
  input  CLK,
  input  [31:0] IM,
  input  [31:0] PC,
  input  [31:0] RegRS,
  input  [31:0] RegRT,
  input  [31:0] OFFSET,
  output [31:0] NextPC,
  output [15:0] unconditional,
  output [15:0] conditional,
  output [15:0] conditionalsucces
);

  wire and_3_out, and_4_out, and_5_out, BEQ, BGTZ, BNE, comparator_1_eq, comparator_2_eq, comparator_3_eq,
       comparator_4_eq, comparator_4_gt, comparator_10_eq, halt, J, JAL, JR, not_1_out, not_2_out, or_3_out,
       or_4_out, syscall;
  wire [1:0] or_2_out;
  wire [31:0] adder_1_out, adder_2_out, multiplexer_1_out, multiplexer_2_out;

  Multiplexer #(.width(32), .enable("false")) multiplexer_1 (
    .in0(RegRT), .in1({32{1'b0}}), .out(multiplexer_1_out), .sel(BGTZ));
  // Probe on PC
  Comparator #(.width(6)) comparator_1 (.a(IM[5:0]), .b(6'b001000), .eq(comparator_1_eq));  // open: gt, lt
  Comparator #(.width(6)) comparator_2 (.a(IM[31:26]), .b({6{1'b0}}), .eq(comparator_2_eq));  // open: gt, lt
  Comparator #(.width(6)) comparator_3 (.a(IM[5:0]), .b(6'b001100), .eq(comparator_3_eq));  // open: gt, lt
  Adder #(.width(32)) adder_1 (.a(PC), .b(32'h4), .out(adder_1_out));  // open: cin, cout
  Multiplexer #(.width(32), .enable("false")) multiplexer_2 (
    .in0({PC[31:28], IM[25:0], 2'b00}), .in1(RegRS), .out(multiplexer_2_out), .sel(JR));
  Adder #(.width(32)) adder_2 (.a({OFFSET[29:0], 2'b00}), .b(adder_1_out), .out(adder_2_out));  // open: cin, cout
  Comparator #(.width(32)) comparator_4 (
    .a(RegRS), .b(multiplexer_1_out), .gt(comparator_4_gt), .eq(comparator_4_eq));  // open: lt
  Comparator #(.width(6)) comparator_5 (.a(IM[31:26]), .b(6'b000010), .eq(J));  // open: gt, lt
  Comparator #(.width(6)) comparator_6 (.a(IM[31:26]), .b(6'b000011), .eq(JAL));  // open: gt, lt
  and and_1 (JR, comparator_1_eq, comparator_2_eq);
  and and_2 (syscall, comparator_2_eq, comparator_3_eq);
  not not_1 (not_1_out, comparator_4_eq);
  and and_3 (and_3_out, BGTZ, comparator_4_gt);
  and and_4 (and_4_out, not_1_out, BNE);
  and and_5 (and_5_out, comparator_4_eq, BEQ);
  Multiplexer #(.select(2), .width(32)) multiplexer_3 (
    .in0(adder_1_out), .in1(adder_2_out), .in2(multiplexer_2_out), .out(NextPC), .sel(or_2_out),
    .en(not_2_out));  // open: in3
  or or_1 (or_2_out[1], J, JAL, JR);
  or or_2 (or_2_out[0], and_3_out, and_4_out, and_5_out);
  Comparator #(.width(6)) comparator_7 (.a(IM[31:26]), .b(6'b000101), .eq(BNE));  // open: gt, lt
  Comparator #(.width(6)) comparator_8 (.a(IM[31:26]), .b(6'b000111), .eq(BGTZ));  // open: gt, lt
  Comparator #(.width(6)) comparator_9 (.a(IM[31:26]), .b(6'b000100), .eq(BEQ));  // open: gt, lt
  Comparator #(.width(32)) comparator_10 (.a(RegRS), .b(32'ha), .eq(comparator_10_eq));  // open: gt, lt
  not not_2 (not_2_out, Reset);
  and and_6 (halt, comparator_10_eq, syscall);
  or or_3 (or_3_out, J, JAL, JR);
  or or_4 (or_4_out, BNE, BGTZ, BEQ);
  Counter #(.width(16), .max('hffff)) counter_1 (
    .count(or_3_out), .Q(unconditional), .clk(CLK), .clr(Reset));  // open: load, D, carry
  Counter #(.width(16), .max('hffff)) counter_2 (
    .count(or_4_out), .Q(conditional), .clk(CLK), .clr(Reset));  // open: load, D, carry
  Counter #(.width(16), .max('hffff)) counter_3 (
    .count(or_2_out[0]), .Q(conditionalsucces), .clk(CLK), .clr(Reset));  // open: load, D, carry

  // Other names for the same wires on the sheet: func[5:0] = IM[5:0]; instr_index[25:0] = IM[25:0];
  //   operate[5:0] = IM[31:26]; 无条件分支指令数[15:0] = unconditional; 有条件分支成功跳转[15:0] = conditionalsucces;
  //   有条件分支指令数[15:0] = conditional
endmodule

module CPO_regs (
  input  [31:0] PC,
  input  RST,
  input  CLK,
  input  IR1,
  input  ERET,
  input  IR2,
  input  IR3,
  output [31:0] pc_2,
  output W1,
  output W2,
  output W3
);

  wire and_1_out, and_2_out, and_3_out, and_4_out, and_5_out, and_6_out, d_ff_1_q, d_ff_2_q, d_ff_3_q,
       decoder_1_out0, decoder_1_out1, decoder_1_out2, IE, IR1_q, IR2_q, IR3_q, not_1_out, or_1_out,
       or_5_out, or_6_out, or_7_out, priority_encoder_1_gs, \中断请求信号 ;
  wire [1:0] nextexp, nowexp;
  wire [31:0] excpc, RETPC;

  Decoder #(.select(2), .enable("false")) decoder_1 (
    .out0(decoder_1_out0), .out1(decoder_1_out1), .out2(decoder_1_out2), .sel(nowexp));  // open: out3
  or or_1 (or_1_out, \中断请求信号 , ERET);
  or or_2 (W1, IR1_q, d_ff_1_q);
  or or_3 (W2, IR2_q, d_ff_2_q);
  or or_4 (W3, IR3_q, d_ff_3_q);
  Register #(.width(32)) register_1 (.D(PC), .en(or_1_out), .Q(RETPC), .clk(CLK), .clr(RST));
  D_Flip_Flop d_ff_1 (.clk(IR1), .D(1'b1), .Q(d_ff_1_q), .reset(IR1_q));  // open: Qn, preset, en
  D_Flip_Flop d_ff_2 (.clk(IR2), .D(1'b1), .Q(d_ff_2_q), .reset(IR2_q));  // open: Qn, preset, en
  D_Flip_Flop d_ff_3 (.clk(IR3), .D(1'b1), .Q(d_ff_3_q), .reset(IR3_q));  // open: Qn, preset, en
  Multiplexer #(.select(2), .width(32), .enable("false")) multiplexer_1 (
    .in0(PC), .in1(RETPC), .in2(excpc), .out(pc_2), .sel({\中断请求信号 , ERET}));  // open: in3
  or or_5 (or_5_out, d_ff_1_q, IR1_q);
  or or_6 (or_6_out, d_ff_2_q, IR2_q);
  or or_7 (or_7_out, d_ff_3_q, IR3_q);
  and and_1 (and_1_out, or_5_out, ~and_2_out);  // AND_Gate
  and and_2 (and_2_out, ERET, decoder_1_out0);
  and and_3 (and_3_out, or_6_out, ~and_4_out);  // AND_Gate
  and and_4 (and_4_out, ERET, decoder_1_out1);
  and and_5 (and_5_out, or_7_out, ~and_6_out);  // AND_Gate
  and and_6 (and_6_out, ERET, decoder_1_out2);
  Register #(.width(1)) register_2 (.D(\中断请求信号 ), .en(or_1_out), .Q(IE), .clk(CLK), .clr(RST));
  D_Flip_Flop u_IR1 (.clk(CLK), .D(and_1_out), .Q(IR1_q));  // open: Qn, preset, en, reset
  D_Flip_Flop u_IR2 (.clk(CLK), .D(and_3_out), .Q(IR2_q));  // open: Qn, preset, en, reset
  D_Flip_Flop u_IR3 (.clk(CLK), .D(and_5_out), .Q(IR3_q));  // open: Qn, preset, en, reset
  Register #(.width(2)) register_3 (.D(nextexp), .en(\中断请求信号 ), .Q(nowexp), .clk(CLK), .clr(RST));
  Priority_Encoder #(.select(2)) priority_encoder_1 (
    .in0(IR1_q), .in1(IR2_q), .in2(IR3_q), .out(nextexp), .gs(priority_encoder_1_gs));  // open: in3, en_out, en_in
  not not_1 (not_1_out, IE);
  and and_7 (\中断请求信号 , priority_encoder_1_gs, not_1_out);
  Multiplexer #(.select(2), .width(32), .enable("false")) multiplexer_2 (
    .in0(32'h312c), .in1(32'h31a4), .in2(32'h321c), .out(excpc), .sel(nextexp));  // open: in3
endmodule
