// Logisim project ideal_cpu_分支预测.circ as structural Verilog: 10 circuits, main circuit cpu
module cpu (
);

  wire and_1_out, and_3_out, and_4_out, and_5_out, and_6_out, Bs, CBsuccess, CBSUCorJ, clk, comparator_1_eq,
       controler_1__16extimm, controler_1_enchange, controler_1_jal, controler_1_lw, controler_1_regwrite,
       controler_1_sextimm, controler_1_sh, controler_1_sw, ex_1_ext_16_2, ex_1_ext_s_2, ex_1_jal_2,
       ex_1_load, ex_1_regwrite_2, ex_1_store, ex_1_store_sh, ext5_sel, GO, halt, id_1_ext_5_2,
       id_1_ext_16_2, id_1_ext_s_2, id_1_jal_2, id_1_lw_2, id_1_regwrite_2, id_1_sh_2, id_1_sw_2, IR1, IR2,
       IR3, JMP, loaduse, mips_ram_1_p3, not_1_out, not_2_out, or_2_out, or_3_out, predict, RST, stop,
       syscall, W1, W2, W3, we;
  wire [1:0] id_1_enchange_2, mips_ram_1_p5, rAconf, rBconf, w_s;
  wire [3:0] controler_1_aluop, id_1_aluop_next_2;
  wire [4:0] rA_t, rB_t, rw;
  wire [15:0] counter_5_q, load_use, multiplexer_12_out, \总周期数 , \插入气泡数 , \无条件分支指令数 , \有条件分支成功跳转 ;
  wire [31:0] adder_1_out, alu_1_result, bht_table_1_npc, bht_table_1_pc_2, bit_extender_1_out,
       bit_extender_2_out, ex_1_im, ex_1_pc, ex_1_regb, ex_1_result, EX_NEXT, ext32, id_1_ext32, id_1_im,
       id_1_pc, id_1_rega, id_1_regb, ID_IM, if_1_pc, jalpc, mem_1_mem, mem_1_result, mips_ram_1_p7,
       multiplexer_4_out, multiplexer_8_out, multiplexer_9_out, multiplexer_10_out, npc_1_nextpc, PC_q, RA,
       RB, registerfile_1_p7, registerfile_1_p8, rom_1_data, SyscallOut;

  Button \u_总复位  (.out(RST));
  Button _1 (.out(IR1));
  Button _2 (.out(IR2));
  Button _3 (.out(IR3));
  Clock clock_1 (.out(clk));
  Button u_GO (.out(GO));
  LED led_1 (.in(W1));
  LED led_2 (.in(W2));
  LED led_3 (.in(W3));
  Comparator #(.width(32)) comparator_1 (.a(RA), .b(32'h22), .eq(comparator_1_eq));  // open: gt, lt
  Hex_Digit_Display hex_digit_display_1 (.value(SyscallOut[31:28]));  // open: dp
  or or_1 (CBSUCorJ, CBsuccess, JMP);
  Multiplexer #(.width(5), .enable("false")) multiplexer_1 (
    .in0(ID_IM[25:21]), .in1(5'b00010), .out(rA_t), .sel(syscall));
  Hex_Digit_Display hex_digit_display_2 (.value(SyscallOut[27:24]));  // open: dp
  Hex_Digit_Display hex_digit_display_3 (.value(SyscallOut[23:20]));  // open: dp
  NPC npc_1 (
    .Reset(RST), .IM(ID_IM), .PC(bht_table_1_npc), .RegRS(RA), .RegRT(RB), .OFFSET(ext32),
    .NextPC(npc_1_nextpc), .CB_success(CBsuccess), .predict(predict), .Bs(Bs), .JMP(JMP));
  nor nor_1 (stop, halt, loaduse);
  and and_1 (and_1_out, ~GO, ~loaduse, ~comparator_1_eq);  // AND_Gate
  and and_2 (halt, and_1_out, syscall);
  Hex_Digit_Display hex_digit_display_4 (.value(SyscallOut[19:16]));  // open: dp
  Hex_Digit_Display hex_digit_display_5 (.value(SyscallOut[15:12]));  // open: dp
  Register #(.width(32)) PC (.D(npc_1_nextpc), .en(stop), .Q(PC_q), .clk(clk), .clr(RST));
  Multiplexer #(.width(5), .enable("false")) multiplexer_2 (
    .in0(ID_IM[20:16]), .in1(5'b00100), .out(rB_t), .sel(syscall));
  Hex_Digit_Display hex_digit_display_6 (.value(SyscallOut[11:8]));  // open: dp
  Hex_Digit_Display hex_digit_display_7 (.value(SyscallOut[7:4]));  // open: dp
  BHT_table bht_table_1 (
    .PC(PC_q), .clk(clk), .rst(RST), .JMP(JMP), .CBSUC(CBsuccess), .npc(bht_table_1_npc),
    .pc_2(bht_table_1_pc_2), .newjmpPC(if_1_pc), .newjmpnextPC(npc_1_nextpc), .predict(predict), .Bs(Bs));
  Hex_Digit_Display hex_digit_display_8 (.value(SyscallOut[3:0]));  // open: dp
  and and_3 (and_3_out, CBSUCorJ, ~predict);  // AND_Gate
  and and_4 (and_4_out, Bs, ~CBSUCorJ, predict);  // AND_Gate
  IF if_1 (
    .pc_4(bht_table_1_pc_2), .next_im(rom_1_data), .CLK(clk), .RST(RST), .pc(if_1_pc), .im(ID_IM),
    .halt(halt), .conflict(loaduse), .CB(or_2_out));
  ROM #(.addrWidth(10), .dataWidth(32)) rom_1 (.addr(bht_table_1_pc_2[11:2]), .data(rom_1_data));  // open: sel
  or or_2 (or_2_out, and_3_out, and_4_out);
  // Probe on \总周期数 
  // Probe on \无条件分支指令数 
  // Probe on load_use
  // Probe on \有条件分支成功跳转 
  // Probe on \插入气泡数 
  and and_5 (and_5_out, CBsuccess, not_1_out);
  not not_1 (not_1_out, loaduse);
  controler controler_1 (
    .AluOp(controler_1_aluop), .LW(controler_1_lw), ._16ExtImm(controler_1__16extimm), .JAL(controler_1_jal),
    .syscall(syscall), .SW(controler_1_sw), .SExtImm(controler_1_sextimm), ._5ExtImm(ext5_sel),
    .RegWrite(controler_1_regwrite), .enchange(controler_1_enchange), .IM(ID_IM), .SH(controler_1_sh));
  Multiplexer #(.width(32), .enable("false")) multiplexer_3 (
    .in0(ID_IM), .in1({32{1'b0}}), .out(EX_NEXT), .sel(loaduse));
  Counter #(.width(16), .max('hffff)) counter_1 (
    .count(and_5_out), .Q(\有条件分支成功跳转 ), .clk(clk), .clr(RST));  // open: load, D, carry
  assign bit_extender_1_out = {{16{ID_IM[15]}}, ID_IM[15:0]};  // Bit_Extender bit_extender_1
  assign bit_extender_2_out = {{27{1'b0}}, ID_IM[10:6]};  // Bit_Extender bit_extender_2
  Adder #(.width(32)) adder_1 (.a(32'h4), .b(jalpc), .out(adder_1_out));  // open: cin, cout
  Multiplexer #(.select(2), .width(32), .enable("false")) multiplexer_4 (
    .in0(mem_1_result), .in1(mem_1_mem), .in2(adder_1_out), .out(multiplexer_4_out), .sel(w_s));  // open: in3
  Multiplexer #(.width(32), .enable("false")) multiplexer_5 (
    .in0(bit_extender_1_out), .in1(bit_extender_2_out), .out(ext32), .sel(ext5_sel));
  Counter #(.width(16), .max('hffff)) counter_2 (
    .count(loaduse), .Q(\插入气泡数 ), .clk(clk), .clr(RST));  // open: load, D, carry
  // RegisterFile registerfile_1: pin names not known; wires that end beside it: multiplexer_4_out, clk, we, rw, rA_t, rB_t, registerfile_1_p7, registerfile_1_p8
  checkconflict checkconflict_1 (
    .rA(rA_t), .IM_EX(id_1_im), .rB(rB_t), .IM_id(ID_IM), .loaduse(loaduse), .MEM_IM(ex_1_im),
    .rAconf(rAconf), .rBconf(rBconf));
  Multiplexer #(.select(2), .width(32), .enable("false")) multiplexer_6 (
    .in0(registerfile_1_p7), .in1(alu_1_result), .in2(multiplexer_10_out), .out(RA), .sel(rAconf));  // open: in3
  Multiplexer #(.select(2), .width(32), .enable("false")) multiplexer_7 (
    .in0(registerfile_1_p8), .in1(alu_1_result), .in2(multiplexer_10_out), .out(RB), .sel(rBconf));  // open: in3
  ID id_1 (
    .ext32_next(ext32), .regA_next(RA), .regB_next(RB), .CLK(clk), .RST(RST), .ext32(id_1_ext32),
    .regA(id_1_rega), .regB(id_1_regb), .aluop_next(controler_1_aluop), .lw(controler_1_lw),
    .sw(controler_1_sw), .ext_5(ext5_sel), .ext_16(controler_1__16extimm), .ext_s(controler_1_sextimm),
    .enchange(controler_1_enchange), .ext_s_2(id_1_ext_s_2), .ext_16_2(id_1_ext_16_2),
    .ext_5_2(id_1_ext_5_2), .sw_2(id_1_sw_2), .lw_2(id_1_lw_2), .enchange_2(id_1_enchange_2[0]),
    .aluop_next_2(id_1_aluop_next_2), .regwrite(controler_1_regwrite), .regwrite_2(id_1_regwrite_2),
    .jal(controler_1_jal), .jal_2(id_1_jal_2), .PC_N(if_1_pc), .pc(id_1_pc), .IM_N(EX_NEXT), .im(id_1_im),
    .halt(halt), .conflict(loaduse), .sh(controler_1_sh), .sh_2(id_1_sh_2));
  Counter #(.width(16), .max('hffff)) counter_3 (
    .count(JMP), .Q(\无条件分支指令数 ), .clk(clk), .clr(RST));  // open: load, D, carry
  or or_3 (or_3_out, id_1_ext_5_2, id_1_enchange_2[0]);
  Multiplexer #(.width(32), .enable("false")) multiplexer_8 (
    .in0(id_1_rega), .in1(id_1_regb), .out(multiplexer_8_out), .sel(or_3_out));
  or or_4 (id_1_enchange_2[1], id_1_ext_s_2, id_1_ext_16_2, id_1_ext_5_2);
  Multiplexer #(.select(2), .width(32), .enable("false")) multiplexer_9 (
    .in0(id_1_regb), .in1(id_1_rega), .in2(id_1_ext32), .out(multiplexer_9_out), .sel(id_1_enchange_2));  // open: in3
  ALU alu_1 (
    .AluOP(id_1_aluop_next_2), .X(multiplexer_8_out), .Result(alu_1_result), .Y(multiplexer_9_out));  // open: Equal, Signed_Overflow, Result_2, UnSigned_Overflow
  Register #(.width(32)) register_1 (.D(RB), .en(and_6_out), .Q(SyscallOut), .clk(clk), .clr(RST));
  and and_6 (and_6_out, syscall, ~halt);  // AND_Gate
  EX ex_1 (
    .sw(id_1_sw_2), .result_next(alu_1_result), .regB_next(id_1_regb), .CLK(clk), .RST(RST),
    .store(ex_1_store), .result(ex_1_result), .regB(ex_1_regb), .lw(id_1_lw_2), .load(ex_1_load),
    .regwrite(id_1_regwrite_2), .regwrite_2(ex_1_regwrite_2), .ext_s(id_1_ext_s_2), .ext_s_2(ex_1_ext_s_2),
    .ext_16(id_1_ext_16_2), .ext_16_2(ex_1_ext_16_2), .jal(id_1_jal_2), .jal_2(ex_1_jal_2), .PC_N(id_1_pc),
    .pc(ex_1_pc), .IM_N(id_1_im), .im(ex_1_im), .halt(halt), .sh(id_1_sh_2), .store_sh(ex_1_store_sh));
  Multiplexer #(.width(32), .enable("false")) multiplexer_10 (
    .in0(ex_1_result), .in1(mips_ram_1_p7), .out(multiplexer_10_out), .sel(ex_1_load));
  // MIPS_RAM mips_ram_1: pin names not known; wires that end beside it: ex_1_result[11:0], ex_1_regb, mips_ram_1_p3, clk, mips_ram_1_p5, RST, mips_ram_1_p7
  or or_5 (mips_ram_1_p3, ex_1_store_sh, ex_1_store);
  Counter #(.width(16), .max('hffff)) counter_4 (
    .count(loaduse), .Q(load_use), .clk(clk), .clr(RST));  // open: load, D, carry
  Multiplexer #(.width(2), .enable("false")) multiplexer_11 (
    .in0(2'b00), .in1(2'b10), .out(mips_ram_1_p5), .sel(ex_1_store_sh));
  MEM mem_1 (
    .mem_next(mips_ram_1_p7), .result_next(ex_1_result), .CLK(clk), .RST(RST), .mem(mem_1_mem),
    .result(mem_1_result), .ext_s(ex_1_ext_s_2), .regw(rw), .ext_16(ex_1_ext_16_2), .jal(ex_1_jal_2),
    .writedata(w_s), .regwrite(ex_1_regwrite_2), .regwrite_2(we), .lw(ex_1_load), .PC_N(ex_1_pc), .pc(jalpc),
    .IM_N(ex_1_im), .halt(halt));
  not not_2 (not_2_out, halt);
  Multiplexer #(.width(16), .enable("false")) multiplexer_12 (
    .in0(16'h4), .in1({16{1'b0}}), .out(multiplexer_12_out), .sel(not_2_out));
  Counter #(.width(16), .max('hffff)) counter_5 (
    .count(not_2_out), .Q(counter_5_q), .clk(clk), .clr(RST));  // open: load, D, carry
  Adder #(.width(16)) adder_2 (.a(multiplexer_12_out), .b(counter_5_q), .out(\总周期数 ));  // open: cin, cout

  // Other names for the same wires on the sheet: Rt[4:0] = ID_IM[20:16]; Rs[4:0] = ID_IM[25:21]

  // Notes on the sheet:
  //   数码管输出应该用寄存器锁存，否则显示数据只能一闪而过
  //   可以通过项目增加Logisim库的方式将前几次实验完成的电路作为子电路引入到本电路中使用
  //   数码管输出
  //   总复位信号应将除ROM以外所有存储组件全部清零
  //   指令存储器
  //   contents of rom_1 (hex, n*v repeats v):
  //   20110001 8000c05 20110001 20120002 20130003 8000c09 20110001 20120002 20130003 8000c0d 20110001
  //   20120002 20130003 8000c11 20110001 20120002 20130003 c000cfa 20100001 20110001 118fc0 112020
  //   20020022 c 118882 12200001 8000c15 112020 20020022 c 20110001 118880 112020 20020022 c 12200001
  //   8000c1f 20110001 118fc0 112020 20020022 c 1188c3 112020 20020022 c 118903 112020 20020022 c 118903
  //   112020 20020022 c 118903 112020 20020022 c 118903 112020 20020022 c 118903 112020 20020022 c 118903
  //   112020 20020022 c 118903 112020 20020022 c 20100001 109fc0 139fc3 8021 2012000c 24160003 26100001
  //   3210000f 20080008 20090001 139900 2709825 132020 20020022 c 1094022 1500fff9 22100001 2018000f
  //   2188024 108700 20080008 20090001 139902 2709825 132021 20020022 c 1094022 1500fff9 108702 2c9b022
  //   12c00001 8000c50 4020 1084027 84400 3508ffff 82021 20020022 c 2010ffff 20110000 ae300000 22100001
  //   22310004 ae300000 22100001 22310004 ae300000 22100001 22310004 ae300000 22100001 22310004 ae300000
  //   22100001 22310004 ae300000 22100001 22310004 ae300000 22100001 22310004 ae300000 22100001 22310004
  //   ae300000 22100001 22310004 ae300000 22100001 22310004 ae300000 22100001 22310004 ae300000 22100001
  //   22310004 ae300000 22100001 22310004 ae300000 22100001 22310004 ae300000 22100001 22310004 ae300000
  //   22100001 22310004 22100001 8020 2011003c 8e130000 8e340000 274402a 11000002 ae330000 ae140000
  //   2231fffc 1611fff8 102020 20020022 c 22100004 2011003c 1611fff2 20020032 c 20080001 20090003 20110876
  //   112020 20020022 c 200b0008 1118804 1318804 112020 20020022 c 216bffff 1560fff9 20020032 c 20080001
  //   20090003 20110876 118d00 112020 20020022 c 200b0008 1118806 1318806 112020 20020022 c 216bffff
  //   1560fff9 20020032 c 20090000 200b0020 20110001 20120001 a5310000 112020 20020022 c 2328820 21290002
  //   216bffff 1560fff8 200b0010 20090000 8d310000 112020 20020022 c 21290004 216bffff 1560fff9 20020032 c
  //   2011000f 112020 20020022 c 2231ffff 1e20fffb 20020032 c 2002000a c 20100000 22100001 102020 20020022
  //   c 22100002 102020 20020022 c 22100003 102020 20020022 c 22100004 102020 20020022 c 22100005 102020
  //   20020022 c 22100006 102020 20020022 c 22100007 102020 20020022 c 22100008 102020 20020022 20020022 c
  //   3e00008
  //   寄存器文件
endmodule

module controler (
  input  [31:0] IM,
  output syscall,
  output _16ExtImm,
  output SExtImm,
  output _5ExtImm,
  output [3:0] AluOp,
  output LW,
  output SW,
  output SH,
  output RegWrite,
  output enchange,
  output JAL
);

  wire ADD, ADDI, ADDIU, ADDU, AND, ANDI, BEQ, BGTZ, BNE, comparator_2_eq, comparator_3_eq, comparator_6_eq,
       comparator_8_eq, comparator_9_eq, comparator_10_eq, comparator_11_eq, comparator_12_eq,
       comparator_13_eq, comparator_15_eq, comparator_16_eq, comparator_17_eq, comparator_19_eq,
       comparator_27_eq, comparator_28_eq, JR, NOR, OR, ORI, R1, SLL, SLLV, SLT, SLTI, SLTU, SRA, SRL, SRLV,
       SUB;
  wire [3:0] and_14_out, and_15_out, and_16_out, and_17_out, and_18_out, and_19_out, and_20_out, and_21_out,
       and_22_out, and_23_out;
  wire [3:3] or_1_out, or_2_out, or_3_out, or_4_out, or_5_out, or_6_out;

  Comparator #(.width(6)) comparator_1 (.a(IM[31:26]), .b({6{1'b0}}), .eq(R1));  // open: gt, lt
  Comparator #(.width(6)) comparator_2 (.a(IM[5:0]), .b(6'b100000), .eq(comparator_2_eq));  // open: gt, lt
  Comparator #(.width(6)) comparator_3 (.a(IM[5:0]), .b(6'b100001), .eq(comparator_3_eq));  // open: gt, lt
  Comparator #(.width(6)) comparator_4 (.a(IM[31:26]), .b(6'b001000), .eq(ADDI));  // open: gt, lt
  Comparator #(.width(6)) comparator_5 (.a(IM[31:26]), .b(6'b001001), .eq(ADDIU));  // open: gt, lt
  Comparator #(.width(6)) comparator_6 (.a(IM[5:0]), .b(6'b100100), .eq(comparator_6_eq));  // open: gt, lt
  Comparator #(.width(6)) comparator_7 (.a(IM[31:26]), .b(6'b001100), .eq(ANDI));  // open: gt, lt
  Comparator #(.width(6)) comparator_8 (.a(IM[5:0]), .b({6{1'b0}}), .eq(comparator_8_eq));  // open: gt, lt
  Comparator #(.width(6)) comparator_9 (.a(IM[5:0]), .b(6'b000100), .eq(comparator_9_eq));  // open: gt, lt
  Comparator #(.width(6)) comparator_10 (.a(IM[5:0]), .b(6'b000010), .eq(comparator_10_eq));  // open: gt, lt
  Comparator #(.width(6)) comparator_11 (.a(IM[5:0]), .b(6'b000110), .eq(comparator_11_eq));  // open: gt, lt
  Comparator #(.width(6)) comparator_12 (.a(IM[5:0]), .b(6'b000011), .eq(comparator_12_eq));  // open: gt, lt
  Comparator #(.width(6)) comparator_13 (.a(IM[5:0]), .b(6'b100101), .eq(comparator_13_eq));  // open: gt, lt
  Comparator #(.width(6)) comparator_14 (.a(IM[31:26]), .b(6'b001101), .eq(ORI));  // open: gt, lt
  Comparator #(.width(6)) comparator_15 (.a(IM[5:0]), .b(6'b100111), .eq(comparator_15_eq));  // open: gt, lt
  Comparator #(.width(6)) comparator_16 (.a(IM[5:0]), .b(6'b101010), .eq(comparator_16_eq));  // open: gt, lt
  Comparator #(.width(6)) comparator_17 (.a(IM[5:0]), .b(6'b101011), .eq(comparator_17_eq));  // open: gt, lt
  Comparator #(.width(6)) comparator_18 (.a(IM[31:26]), .b(6'b001010), .eq(SLTI));  // open: gt, lt
  Comparator #(.width(6)) comparator_19 (.a(IM[5:0]), .b(6'b100010), .eq(comparator_19_eq));  // open: gt, lt
  Comparator #(.width(6)) comparator_20 (.a(IM[31:26]), .b(6'b000101), .eq(BNE));  // open: gt, lt
  Comparator #(.width(6)) comparator_21 (.a(IM[31:26]), .b(6'b000111), .eq(BGTZ));  // open: gt, lt
  Comparator #(.width(6)) comparator_22 (.a(IM[31:26]), .b(6'b000100), .eq(BEQ));  // open: gt, lt
  Comparator #(.width(6)) comparator_23 (.a(IM[31:26]), .b(6'b100011), .eq(LW));  // open: gt, lt
  Comparator #(.width(6)) comparator_24 (.a(IM[31:26]), .b(6'b101011), .eq(SW));  // open: gt, lt
  Comparator #(.width(6)) comparator_25 (.a(IM[31:26]), .b(6'b101001), .eq(SH));  // open: gt, lt
  and and_1 (ADD, R1, comparator_2_eq);
  and and_2 (ADDU, R1, comparator_3_eq);
  and and_3 (AND, R1, comparator_6_eq);
  and and_4 (SLL, R1, comparator_8_eq);
  and and_5 (SLLV, R1, comparator_9_eq);
  and and_6 (SRL, R1, comparator_10_eq);
  and and_7 (SRLV, R1, comparator_11_eq);
  and and_8 (SRA, R1, comparator_12_eq);
  and and_9 (OR, R1, comparator_13_eq);
  and and_10 (NOR, R1, comparator_15_eq);
  and and_11 (SLT, R1, comparator_16_eq);
  and and_12 (SLTU, R1, comparator_17_eq);
  and and_13 (SUB, R1, comparator_19_eq);
  or or_1 (or_1_out[3], ADD, ADDI, ADDU, ADDIU, SW, LW, SH);
  or or_2 (or_2_out[3], AND, ANDI);
  or or_3 (or_3_out[3], OR, ORI);
  or or_4 (or_4_out[3], SLL, SLLV);
  or or_5 (or_5_out[3], SLT, SLTI);
  or or_6 (or_6_out[3], SRL, SRLV);
  Comparator #(.width(6)) comparator_26 (.a(IM[31:26]), .b(6'b000011), .eq(JAL));  // open: gt, lt
  Comparator #(.width(6)) comparator_27 (.a(IM[5:0]), .b(6'b001000), .eq(comparator_27_eq));  // open: gt, lt
  Comparator #(.width(6)) comparator_28 (.a(IM[5:0]), .b(6'b001100), .eq(comparator_28_eq));  // open: gt, lt
  assign and_14_out = 4'b0101 & {4{or_1_out[3]}};  // AND_Gate and_14, 4 bits wide
  assign and_15_out = 4'b0111 & {4{or_2_out[3]}};  // AND_Gate and_15, 4 bits wide
  assign and_16_out = 4'b1000 & {4{or_3_out[3]}};  // AND_Gate and_16, 4 bits wide
  assign and_17_out = 4'b0000 & {4{or_4_out[3]}};  // AND_Gate and_17, 4 bits wide
  assign and_18_out = 4'b1010 & {4{NOR}};  // AND_Gate and_18, 4 bits wide
  assign and_19_out = 4'b0001 & {4{SRA}};  // AND_Gate and_19, 4 bits wide
  assign and_20_out = 4'b1011 & {4{or_5_out[3]}};  // AND_Gate and_20, 4 bits wide
  assign and_21_out = 4'b1100 & {4{SLTU}};  // AND_Gate and_21, 4 bits wide
  assign and_22_out = 4'b0110 & {4{SUB}};  // AND_Gate and_22, 4 bits wide
  assign and_23_out = 4'b0010 & {4{or_6_out[3]}};  // AND_Gate and_23, 4 bits wide
  and and_24 (JR, R1, comparator_27_eq);
  and and_25 (syscall, R1, comparator_28_eq);
  assign AluOp = and_14_out | and_15_out | and_16_out | and_17_out | and_18_out | and_19_out | and_20_out | and_21_out | and_22_out | and_23_out;  // OR_Gate or_7, 4 bits wide
  or or_8 (_16ExtImm, ANDI, ORI);
  or or_9 (SExtImm, ADDI, ADDIU, LW, SW, SH, BNE, BGTZ, BEQ, SLTI);
  or or_10 (_5ExtImm, SLL, SRA, SRL);
  or or_11 (enchange, SRLV, SLLV);
  or or_12 (RegWrite, SRLV, ADD, ADDU, ADDI, ADDIU, AND, ANDI, SLL, SLLV, SRL, SRA, OR, ORI, NOR, SLT, SLTU, SLTI, SUB, JAL, LW);

  // Other names for the same wires on the sheet: func[5:0] = IM[5:0]; operate[5:0] = IM[31:26]; sllv_srlv = enchange
endmodule

module NPC (
  input  Reset,
  input  predict,
  input  [31:0] IM,
  input  [31:0] PC,
  input  [31:0] RegRS,
  input  [31:0] RegRT,
  input  [31:0] OFFSET,
  output [31:0] NextPC,
  output CB_success,
  output Bs,
  output JMP
);

  wire and_2_out, and_3_out, and_4_out, BEQ, BGTZ, BNE, comparator_1_eq, comparator_2_eq, comparator_3_eq,
       comparator_3_gt, J, JAL, JR, not_1_out, not_2_out, or_1_out;
  wire [1:0] and_5_out;
  wire [31:0] adder_1_out, multiplexer_1_out, multiplexer_2_out, subtractor_1_out;

  // Probe on IM
  // Probe on PC
  Multiplexer #(.width(32), .enable("false")) multiplexer_1 (
    .in0(RegRT), .in1({32{1'b0}}), .out(multiplexer_1_out), .sel(BGTZ));
  Comparator #(.width(6)) comparator_1 (.a(IM[5:0]), .b(6'b001000), .eq(comparator_1_eq));  // open: gt, lt
  Comparator #(.width(6)) comparator_2 (.a(IM[31:26]), .b({6{1'b0}}), .eq(comparator_2_eq));  // open: gt, lt
  Subtractor #(.width(32)) subtractor_1 (.a(PC), .b(32'h4), .out(subtractor_1_out));  // open: bin, bout
  Multiplexer #(.width(32), .enable("false")) multiplexer_2 (
    .in0({PC[31:28], IM[25:0], 2'b00}), .in1(RegRS), .out(multiplexer_2_out), .sel(JR));
  Comparator #(.width(32), .mode("unsigned")) comparator_3 (
    .a(RegRS), .b(multiplexer_1_out), .gt(comparator_3_gt), .eq(comparator_3_eq));  // open: lt
  Comparator #(.width(6)) comparator_4 (.a(IM[31:26]), .b(6'b000010), .eq(J));  // open: gt, lt
  Comparator #(.width(6)) comparator_5 (.a(IM[31:26]), .b(6'b000011), .eq(JAL));  // open: gt, lt
  and and_1 (JR, comparator_1_eq, comparator_2_eq);
  Adder #(.width(32)) adder_1 (.a(subtractor_1_out), .b({OFFSET[29:0], 2'b00}), .out(adder_1_out));  // open: cin, cout
  not not_1 (not_1_out, comparator_3_eq);
  // Probe on PC
  and and_2 (and_2_out, BGTZ, comparator_3_gt);
  and and_3 (and_3_out, not_1_out, BNE);
  and and_4 (and_4_out, comparator_3_eq, BEQ);
  Multiplexer #(.select(2), .width(32)) multiplexer_3 (
    .in0(PC), .in1(adder_1_out), .in2(multiplexer_2_out), .out(NextPC), .sel(and_5_out), .en(not_2_out));  // open: in3
  and and_5 (and_5_out[0], CB_success, ~predict);  // AND_Gate
  and and_6 (and_5_out[1], or_1_out, ~predict);  // AND_Gate
  or or_1 (or_1_out, J, JAL, JR);
  or or_2 (CB_success, and_2_out, and_3_out, and_4_out);
  Comparator #(.width(6)) comparator_6 (.a(IM[31:26]), .b(6'b000101), .eq(BNE));  // open: gt, lt
  Comparator #(.width(6)) comparator_7 (.a(IM[31:26]), .b(6'b000111), .eq(BGTZ));  // open: gt, lt
  Comparator #(.width(6)) comparator_8 (.a(IM[31:26]), .b(6'b000100), .eq(BEQ));  // open: gt, lt
  // Probe on NextPC
  not not_2 (not_2_out, Reset);
  // Probe on NextPC
  or or_3 (Bs, BNE, BGTZ, BEQ);
  or or_4 (JMP, J, JAL, JR);

  // Other names for the same wires on the sheet: func[5:0] = IM[5:0]; instr_index[25:0] = IM[25:0];
  //   operate[5:0] = IM[31:26]
endmodule

module IF (
  input  [31:0] pc_4,
  input  [31:0] next_im,
  input  CLK,
  input  RST,
  input  halt,
  input  conflict,
  input  CB,
  output [31:0] pc,
  output [31:0] im
);

  wire nor_1_out;
  wire [31:0] multiplexer_1_out, multiplexer_2_out;

  Multiplexer #(.width(32), .enable("false")) multiplexer_1 (
    .in0(pc_4), .in1({32{1'b0}}), .out(multiplexer_1_out), .sel(CB));
  nor nor_1 (nor_1_out, halt, conflict);
  Multiplexer #(.width(32), .enable("false")) multiplexer_2 (
    .in0(next_im), .in1({32{1'b0}}), .out(multiplexer_2_out), .sel(CB));
  Register #(.width(32)) register_1 (.D(multiplexer_1_out), .en(nor_1_out), .Q(pc), .clk(CLK), .clr(RST));
  Register #(.width(32)) register_2 (.D(multiplexer_2_out), .en(nor_1_out), .Q(im), .clk(CLK), .clr(RST));
endmodule

module ID (
  input  [31:0] PC_N,
  input  [31:0] IM_N,
  input  [31:0] ext32_next,
  input  [31:0] regA_next,
  input  [31:0] regB_next,
  input  ext_s,
  input  ext_16,
  input  ext_5,
  input  sh,
  input  sw,
  input  lw,
  input  regwrite,
  input  jal,
  input  enchange,
  input  [3:0] aluop_next,
  input  CLK,
  input  RST,
  input  halt,
  input  conflict,
  output [31:0] pc,
  output [31:0] im,
  output [31:0] ext32,
  output [31:0] regA,
  output [31:0] regB,
  output ext_s_2,
  output ext_16_2,
  output ext_5_2,
  output sh_2,
  output sw_2,
  output lw_2,
  output regwrite_2,
  output jal_2,
  output enchange_2,
  output [3:0] aluop_next_2
);

  wire and_1_out, and_2_out, and_3_out, and_4_out, and_5_out, and_6_out, and_7_out, and_8_out, and_9_out,
       not_1_out, not_2_out;
  wire [3:0] multiplexer_1_out;

  not not_1 (not_1_out, halt);
  not not_2 (not_2_out, conflict);
  and and_1 (and_1_out, ext_s, not_2_out);
  and and_2 (and_2_out, ext_16, not_2_out);
  and and_3 (and_3_out, ext_5, not_2_out);
  and and_4 (and_4_out, sh, not_2_out);
  and and_5 (and_5_out, sw, not_2_out);
  and and_6 (and_6_out, lw, not_2_out);
  and and_7 (and_7_out, regwrite, not_2_out);
  and and_8 (and_8_out, jal, not_2_out);
  and and_9 (and_9_out, enchange, not_2_out);
  Multiplexer #(.width(4), .enable("false")) multiplexer_1 (
    .in0(4'b0000), .in1(aluop_next), .out(multiplexer_1_out), .sel(not_2_out));
  Register #(.width(1)) register_1 (.D(and_1_out), .en(not_1_out), .Q(ext_s_2), .clk(CLK), .clr(RST));
  Register #(.width(1)) register_2 (.D(and_3_out), .en(not_1_out), .Q(ext_5_2), .clk(CLK), .clr(RST));
  Register #(.width(1)) register_3 (.D(and_5_out), .en(not_1_out), .Q(sw_2), .clk(CLK), .clr(RST));
  Register #(.width(1)) register_4 (.D(and_7_out), .en(not_1_out), .Q(regwrite_2), .clk(CLK), .clr(RST));
  Register #(.width(1)) register_5 (.D(and_9_out), .en(not_1_out), .Q(enchange_2), .clk(CLK), .clr(RST));
  Register #(.width(32)) register_6 (.D(PC_N), .en(not_1_out), .Q(pc), .clk(CLK), .clr(RST));
  Register #(.width(32)) register_7 (.D(IM_N), .en(not_1_out), .Q(im), .clk(CLK), .clr(RST));
  Register #(.width(32)) register_8 (.D(ext32_next), .en(not_1_out), .Q(ext32), .clk(CLK), .clr(RST));
  Register #(.width(32)) register_9 (.D(regA_next), .en(not_1_out), .Q(regA), .clk(CLK), .clr(RST));
  Register #(.width(32)) register_10 (.D(regB_next), .en(not_1_out), .Q(regB), .clk(CLK), .clr(RST));
  Register #(.width(1)) register_11 (.D(and_2_out), .en(not_1_out), .Q(ext_16_2), .clk(CLK), .clr(RST));
  Register #(.width(1)) register_12 (.D(and_4_out), .en(not_1_out), .Q(sh_2), .clk(CLK), .clr(RST));
  Register #(.width(1)) register_13 (.D(and_6_out), .en(not_1_out), .Q(lw_2), .clk(CLK), .clr(RST));
  Register #(.width(1)) register_14 (.D(and_8_out), .en(not_1_out), .Q(jal_2), .clk(CLK), .clr(RST));
  Register #(.width(4)) register_15 (.D(multiplexer_1_out), .en(not_1_out), .Q(aluop_next_2), .clk(CLK), .clr(RST));
endmodule

module EX (
  input  ext_s,
  input  ext_16,
  input  jal,
  input  regwrite,
  input  lw,
  input  sw,
  input  sh,
  input  [31:0] PC_N,
  input  [31:0] IM_N,
  input  [31:0] result_next,
  input  [31:0] regB_next,
  input  CLK,
  input  RST,
  input  halt,
  output ext_s_2,
  output ext_16_2,
  output jal_2,
  output regwrite_2,
  output load,
  output store,
  output store_sh,
  output [31:0] pc,
  output [31:0] im,
  output [31:0] result,
  output [31:0] regB
);

  wire not_1_out;

  not not_1 (not_1_out, halt);
  Register #(.width(1)) register_1 (.D(ext_s), .en(not_1_out), .Q(ext_s_2), .clk(CLK), .clr(RST));
  Register #(.width(1)) register_2 (.D(ext_16), .en(not_1_out), .Q(ext_16_2), .clk(CLK), .clr(RST));
  Register #(.width(1)) register_3 (.D(jal), .en(not_1_out), .Q(jal_2), .clk(CLK), .clr(RST));
  Register #(.width(1)) register_4 (.D(regwrite), .en(not_1_out), .Q(regwrite_2), .clk(CLK), .clr(RST));
  Register #(.width(1)) register_5 (.D(lw), .en(not_1_out), .Q(load), .clk(CLK), .clr(RST));
  Register #(.width(1)) register_6 (.D(sw), .en(not_1_out), .Q(store), .clk(CLK), .clr(RST));
  Register #(.width(1)) register_7 (.D(sh), .en(not_1_out), .Q(store_sh), .clk(CLK), .clr(RST));
  Register #(.width(32)) register_8 (.D(PC_N), .en(not_1_out), .Q(pc), .clk(CLK), .clr(RST));
  Register #(.width(32)) register_9 (.D(IM_N), .en(not_1_out), .Q(im), .clk(CLK), .clr(RST));
  Register #(.width(32)) register_10 (.D(result_next), .en(not_1_out), .Q(result), .clk(CLK), .clr(RST));
  Register #(.width(32)) register_11 (.D(regB_next), .en(not_1_out), .Q(regB), .clk(CLK), .clr(RST));
endmodule

module MEM (
  input  ext_s,
  input  ext_16,
  input  lw,
  input  jal,
  input  regwrite,
  input  [31:0] PC_N,
  input  [31:0] IM_N,
  input  [31:0] mem_next,
  input  [31:0] result_next,
  input  CLK,
  input  RST,
  input  halt,
  output [4:0] regw,
  output [1:0] writedata,
  output regwrite_2,
  output [31:0] pc,
  output [31:0] mem,
  output [31:0] result
);

  wire not_1_out;
  wire [0:0] or_1_out;
  wire [4:0] multiplexer_1_out;

  or or_1 (or_1_out[0], ext_s, ext_16);
  // Probe on IM_N
  not not_1 (not_1_out, halt);
  Multiplexer #(.select(2), .width(5), .enable("false")) multiplexer_1 (
    .in0(IM_N[15:11]), .in1(IM_N[20:16]), .in2({5{1'b1}}), .out(multiplexer_1_out), .sel({jal, or_1_out[0]}));  // open: in3
  Register #(.width(5)) register_1 (.D(multiplexer_1_out), .en(not_1_out), .Q(regw), .clk(CLK), .clr(RST));
  Register #(.width(2)) register_2 (.D({jal, lw}), .en(not_1_out), .Q(writedata), .clk(CLK), .clr(RST));
  Register #(.width(1)) register_3 (.D(regwrite), .en(not_1_out), .Q(regwrite_2), .clk(CLK), .clr(RST));
  Register #(.width(32)) register_4 (.D(PC_N), .en(not_1_out), .Q(pc), .clk(CLK), .clr(RST));
  Register #(.width(32)) register_5 (.D(mem_next), .en(not_1_out), .Q(mem), .clk(CLK), .clr(RST));
  Register #(.width(32)) register_6 (.D(result_next), .en(not_1_out), .Q(result), .clk(CLK), .clr(RST));

  // Other names for the same wires on the sheet: IM[31:0] = IM_N
endmodule

module checkconflict (
  input  [4:0] rA,
  input  [31:0] IM_EX,
  input  [31:0] MEM_IM,
  input  [4:0] rB,
  input  [31:0] IM_id,
  output loaduse,
  output [1:0] rAconf,
  output [1:0] rBconf
);

  wire ADD, ADD_id, ADD_mem, ADDI, ADDI_id, ADDI_mem, ADDIU, ADDIU_id, ADDIU_mem, ADDU, ADDU_id, ADDU_mem,
       AND, and_17_out, and_18_out, and_19_out, and_20_out, and_21_out, and_22_out, and_23_out, and_24_out,
       and_25_out, and_30_out, and_47_out, AND_id, AND_mem, ANDI, ANDI_id, ANDI_mem, BEQ_id, BGTZ_id, BNE_id,
       comparator_1_eq, comparator_2_eq, comparator_3_eq, comparator_4_eq, comparator_5_eq, comparator_6_eq,
       comparator_8_eq, comparator_9_eq, comparator_10_eq, comparator_11_eq, comparator_12_eq,
       comparator_13_eq, comparator_14_eq, comparator_15_eq, comparator_16_eq, comparator_17_eq,
       comparator_18_eq, comparator_19_eq, comparator_20_eq, comparator_21_eq, comparator_22_eq,
       comparator_36_eq, comparator_37_eq, comparator_38_eq, comparator_40_eq, comparator_41_eq,
       comparator_42_eq, comparator_43_eq, comparator_44_eq, comparator_45_eq, comparator_46_eq,
       comparator_47_eq, comparator_48_eq, comparator_49_eq, comparator_50_eq, comparator_51_eq,
       comparator_52_eq, comparator_60_eq, comparator_61_eq, comparator_62_eq, comparator_63_eq,
       comparator_64_eq, comparator_65_eq, comparator_66_eq, comparator_67_eq, comparator_68_eq,
       comparator_69_eq, comparator_70_eq, comparator_71_eq, comparator_72_eq, ex_conflict, J_id, JAL_id,
       JR_id, LW, LW_id, LW_mem, mem_conflict, NOR, NOR_id, NOR_mem, not_1_out, not_2_out, not_3_out,
       not_4_out, OR, or_1_out, or_2_out, or_4_out, or_5_out, OR_id, OR_mem, ORI, ORI_id, ORI_mem, R1, R1_id,
       R1_mem, rA_conf1, rA_conf2, rB_conf1, rB_conf2, reg1_rs, reg1_rt, reg2, reg_rd, reg_rd_mem, reg_rt,
       reg_rt_mem, SH_id, SLL, SLL_mem, SLLV, SLLV_id, SLLV_mem, SLT, SLT_id, SLT_mem, SLTI, SLTI_id,
       SLTI_mem, SLTU, SLTU_id, SLTU_mem, SRA, SRA_mem, SRL, SRL_mem, SRLV, SRLV_id, SRLV_mem, SUB, SUB_id,
       SUB_mem, SW_id, syscall_id;
  wire [4:0] regex, regex_mem;

  Comparator #(.width(5), .mode("unsigned")) comparator_1 (
    .a(rB), .b({5{1'b0}}), .eq(comparator_1_eq));  // open: gt, lt
  Comparator #(.width(5), .mode("unsigned")) comparator_2 (.a(regex), .b(rB), .eq(comparator_2_eq));  // open: gt, lt
  Comparator #(.width(5), .mode("unsigned")) comparator_3 (.a(regex), .b(rA), .eq(comparator_3_eq));  // open: gt, lt
  Comparator #(.width(5), .mode("unsigned")) comparator_4 (
    .a(regex_mem), .b(rB), .eq(comparator_4_eq));  // open: gt, lt
  Comparator #(.width(5), .mode("unsigned")) comparator_5 (
    .a(regex_mem), .b(rA), .eq(comparator_5_eq));  // open: gt, lt
  Comparator #(.width(5), .mode("unsigned")) comparator_6 (
    .a(rA), .b({5{1'b0}}), .eq(comparator_6_eq));  // open: gt, lt
  Comparator #(.width(6)) comparator_7 (.a(IM_id[31:26]), .b({6{1'b0}}), .eq(R1_id));  // open: gt, lt
  Comparator #(.width(6)) comparator_8 (.a(IM_id[5:0]), .b(6'b100000), .eq(comparator_8_eq));  // open: gt, lt
  Comparator #(.width(6)) comparator_9 (.a(IM_id[5:0]), .b(6'b100001), .eq(comparator_9_eq));  // open: gt, lt
  Comparator #(.width(6)) comparator_10 (.a(IM_id[5:0]), .b(6'b100100), .eq(comparator_10_eq));  // open: gt, lt
  Comparator #(.width(6)) comparator_11 (.a(IM_id[5:0]), .b(6'b000100), .eq(comparator_11_eq));  // open: gt, lt
  Comparator #(.width(6)) comparator_12 (.a(IM_id[5:0]), .b(6'b000110), .eq(comparator_12_eq));  // open: gt, lt
  Comparator #(.width(6)) comparator_13 (.a(IM_id[5:0]), .b(6'b100101), .eq(comparator_13_eq));  // open: gt, lt
  Comparator #(.width(6)) comparator_14 (.a(IM_id[5:0]), .b(6'b100111), .eq(comparator_14_eq));  // open: gt, lt
  Comparator #(.width(6)) comparator_15 (.a(IM_id[5:0]), .b(6'b101010), .eq(comparator_15_eq));  // open: gt, lt
  Comparator #(.width(6)) comparator_16 (.a(IM_id[5:0]), .b(6'b101011), .eq(comparator_16_eq));  // open: gt, lt
  Comparator #(.width(6)) comparator_17 (.a(IM_id[5:0]), .b(6'b100010), .eq(comparator_17_eq));  // open: gt, lt
  Comparator #(.width(6)) comparator_18 (.a(IM_id[5:0]), .b(6'b001000), .eq(comparator_18_eq));  // open: gt, lt
  Comparator #(.width(6)) comparator_19 (.a(IM_id[5:0]), .b(6'b001100), .eq(comparator_19_eq));  // open: gt, lt
  and and_1 (rB_conf1, ~comparator_1_eq, comparator_2_eq);  // AND_Gate
  and and_2 (rA_conf1, ~comparator_6_eq, comparator_3_eq);  // AND_Gate
  and and_3 (rB_conf2, ~comparator_1_eq, comparator_4_eq);  // AND_Gate
  and and_4 (rA_conf2, ~comparator_6_eq, comparator_5_eq);  // AND_Gate
  and and_5 (ADD_id, R1_id, comparator_8_eq);
  and and_6 (ADDU_id, R1_id, comparator_9_eq);
  and and_7 (AND_id, R1_id, comparator_10_eq);
  and and_8 (SLLV_id, R1_id, comparator_11_eq);
  and and_9 (SRLV_id, R1_id, comparator_12_eq);
  and and_10 (OR_id, R1_id, comparator_13_eq);
  and and_11 (NOR_id, R1_id, comparator_14_eq);
  and and_12 (SLT_id, R1_id, comparator_15_eq);
  and and_13 (SLTU_id, R1_id, comparator_16_eq);
  and and_14 (SUB_id, R1_id, comparator_17_eq);
  and and_15 (JR_id, R1_id, comparator_18_eq);
  and and_16 (syscall_id, R1_id, comparator_19_eq);
  or or_1 (or_1_out, rB_conf1, rA_conf1);
  or or_2 (or_2_out, rB_conf2, rA_conf2);
  or or_3 (reg2, ADD_id, ADDU_id, AND_id, SLLV_id, SRLV_id, OR_id, syscall_id, SW_id, SH_id, BEQ_id, BNE_id, NOR_id, SLT_id, SLTU_id, SUB_id, JR_id);
  and and_17 (and_17_out, reg1_rt, rB_conf1);
  and and_18 (and_18_out, reg2, or_1_out);
  and and_19 (and_19_out, reg1_rs, rA_conf1);
  and and_20 (and_20_out, reg2, or_2_out);
  and and_21 (and_21_out, reg1_rs, rA_conf2);
  and and_22 (and_22_out, reg1_rt, rB_conf2);
  Comparator #(.width(6)) comparator_20 (.a(IM_id[5:0]), .b({6{1'b0}}), .eq(comparator_20_eq));  // open: gt, lt
  Comparator #(.width(6)) comparator_21 (.a(IM_id[5:0]), .b(6'b000010), .eq(comparator_21_eq));  // open: gt, lt
  Comparator #(.width(6)) comparator_22 (.a(IM_id[5:0]), .b(6'b000011), .eq(comparator_22_eq));  // open: gt, lt
  or or_4 (or_4_out, and_17_out, and_18_out, and_19_out);
  or or_5 (or_5_out, and_20_out, and_21_out, and_22_out);
  and and_23 (and_23_out, R1_id, comparator_20_eq);
  and and_24 (and_24_out, R1_id, comparator_21_eq);
  and and_25 (and_25_out, R1_id, comparator_22_eq);
  Comparator #(.width(6)) comparator_23 (.a(IM_id[31:26]), .b(6'b001000), .eq(ADDI_id));  // open: gt, lt
  Comparator #(.width(6)) comparator_24 (.a(IM_id[31:26]), .b(6'b001001), .eq(ADDIU_id));  // open: gt, lt
  Comparator #(.width(6)) comparator_25 (.a(IM_id[31:26]), .b(6'b001100), .eq(ANDI_id));  // open: gt, lt
  Comparator #(.width(6)) comparator_26 (.a(IM_id[31:26]), .b(6'b001101), .eq(ORI_id));  // open: gt, lt
  Comparator #(.width(6)) comparator_27 (.a(IM_id[31:26]), .b(6'b001010), .eq(SLTI_id));  // open: gt, lt
  Comparator #(.width(6)) comparator_28 (.a(IM_id[31:26]), .b(6'b100011), .eq(LW_id));  // open: gt, lt
  Comparator #(.width(6)) comparator_29 (.a(IM_id[31:26]), .b(6'b101011), .eq(SW_id));  // open: gt, lt
  Comparator #(.width(6)) comparator_30 (.a(IM_id[31:26]), .b(6'b101001), .eq(SH_id));  // open: gt, lt
  Comparator #(.width(6)) comparator_31 (.a(IM_id[31:26]), .b(6'b000101), .eq(BNE_id));  // open: gt, lt
  Comparator #(.width(6)) comparator_32 (.a(IM_id[31:26]), .b(6'b000111), .eq(BGTZ_id));  // open: gt, lt
  Comparator #(.width(6)) comparator_33 (.a(IM_id[31:26]), .b(6'b000100), .eq(BEQ_id));  // open: gt, lt
  Comparator #(.width(6)) comparator_34 (.a(IM_id[31:26]), .b(6'b000010), .eq(J_id));  // open: gt, lt
  Comparator #(.width(6)) comparator_35 (.a(IM_id[31:26]), .b(6'b000011), .eq(JAL_id));  // open: gt, lt
  Comparator #(.width(6)) comparator_36 (.a(IM_id[5:0]), .b(6'b001000), .eq(comparator_36_eq));  // open: gt, lt
  or or_6 (reg1_rt, and_23_out, and_24_out, and_25_out);
  or or_7 (reg1_rs, ADDI_id, ADDIU_id, ANDI_id, ORI_id, SLTI_id, LW_id, BGTZ_id);
  and and_26 (JR_id, R1_id, comparator_36_eq);
  Comparator #(.width(32), .mode("unsigned")) comparator_37 (
    .a(IM_EX), .b({32{1'b0}}), .eq(comparator_37_eq));  // open: gt, lt
  Comparator #(.width(32), .mode("unsigned")) comparator_38 (
    .a(MEM_IM), .b({32{1'b0}}), .eq(comparator_38_eq));  // open: gt, lt
  not not_1 (not_1_out, comparator_37_eq);
  and and_27 (ex_conflict, not_1_out, or_4_out);
  and and_28 (mem_conflict, or_5_out, not_2_out);
  not not_2 (not_2_out, comparator_38_eq);
  and and_29 (rBconf[0], ex_conflict, rB_conf1);
  not not_3 (not_3_out, rBconf[0]);
  and and_30 (and_30_out, rB_conf2, mem_conflict);
  and and_31 (rBconf[1], not_3_out, and_30_out);
  Comparator #(.width(6)) comparator_39 (.a(IM_EX[31:26]), .b({6{1'b0}}), .eq(R1));  // open: gt, lt
  Comparator #(.width(6)) comparator_40 (.a(IM_EX[5:0]), .b(6'b100000), .eq(comparator_40_eq));  // open: gt, lt
  Comparator #(.width(6)) comparator_41 (.a(IM_EX[5:0]), .b(6'b100001), .eq(comparator_41_eq));  // open: gt, lt
  Comparator #(.width(6)) comparator_42 (.a(IM_EX[5:0]), .b(6'b100100), .eq(comparator_42_eq));  // open: gt, lt
  Comparator #(.width(6)) comparator_43 (.a(IM_EX[5:0]), .b({6{1'b0}}), .eq(comparator_43_eq));  // open: gt, lt
  Comparator #(.width(6)) comparator_44 (.a(IM_EX[5:0]), .b(6'b000100), .eq(comparator_44_eq));  // open: gt, lt
  Comparator #(.width(6)) comparator_45 (.a(IM_EX[5:0]), .b(6'b000010), .eq(comparator_45_eq));  // open: gt, lt
  Comparator #(.width(6)) comparator_46 (.a(IM_EX[5:0]), .b(6'b000110), .eq(comparator_46_eq));  // open: gt, lt
  Comparator #(.width(6)) comparator_47 (.a(IM_EX[5:0]), .b(6'b000011), .eq(comparator_47_eq));  // open: gt, lt
  Comparator #(.width(6)) comparator_48 (.a(IM_EX[5:0]), .b(6'b100101), .eq(comparator_48_eq));  // open: gt, lt
  Comparator #(.width(6)) comparator_49 (.a(IM_EX[5:0]), .b(6'b100111), .eq(comparator_49_eq));  // open: gt, lt
  Comparator #(.width(6)) comparator_50 (.a(IM_EX[5:0]), .b(6'b101010), .eq(comparator_50_eq));  // open: gt, lt
  Comparator #(.width(6)) comparator_51 (.a(IM_EX[5:0]), .b(6'b101011), .eq(comparator_51_eq));  // open: gt, lt
  Comparator #(.width(6)) comparator_52 (.a(IM_EX[5:0]), .b(6'b100010), .eq(comparator_52_eq));  // open: gt, lt
  and and_32 (loaduse, ex_conflict, LW);
  or or_8 (reg_rd, ADD, ADDU, AND, SLL, SLLV, SRL, SRLV, SRA, OR, NOR, SLT, SLTU, SUB);
  and and_33 (ADD, R1, comparator_40_eq);
  and and_34 (ADDU, R1, comparator_41_eq);
  and and_35 (AND, R1, comparator_42_eq);
  and and_36 (SLL, R1, comparator_43_eq);
  and and_37 (SLLV, R1, comparator_44_eq);
  and and_38 (SRL, R1, comparator_45_eq);
  and and_39 (SRLV, R1, comparator_46_eq);
  and and_40 (SRA, R1, comparator_47_eq);
  and and_41 (OR, R1, comparator_48_eq);
  and and_42 (NOR, R1, comparator_49_eq);
  and and_43 (SLT, R1, comparator_50_eq);
  and and_44 (SLTU, R1, comparator_51_eq);
  and and_45 (SUB, R1, comparator_52_eq);
  Multiplexer #(.select(2), .width(5), .enable("false")) multiplexer_1 (
    .in0({5{1'b0}}), .in1(IM_EX[15:11]), .in2(IM_EX[20:16]), .in3({5{1'b0}}), .out(regex),
    .sel({reg_rt, reg_rd}));
  and and_46 (rAconf[0], ex_conflict, rA_conf1);
  not not_4 (not_4_out, rAconf[0]);
  and and_47 (and_47_out, rA_conf2, mem_conflict);
  Comparator #(.width(6)) comparator_53 (.a(IM_EX[31:26]), .b(6'b001000), .eq(ADDI));  // open: gt, lt
  Comparator #(.width(6)) comparator_54 (.a(IM_EX[31:26]), .b(6'b001001), .eq(ADDIU));  // open: gt, lt
  Comparator #(.width(6)) comparator_55 (.a(IM_EX[31:26]), .b(6'b001100), .eq(ANDI));  // open: gt, lt
  Comparator #(.width(6)) comparator_56 (.a(IM_EX[31:26]), .b(6'b001101), .eq(ORI));  // open: gt, lt
  Comparator #(.width(6)) comparator_57 (.a(IM_EX[31:26]), .b(6'b001010), .eq(SLTI));  // open: gt, lt
  Comparator #(.width(6)) comparator_58 (.a(IM_EX[31:26]), .b(6'b100011), .eq(LW));  // open: gt, lt
  and and_48 (rAconf[1], not_4_out, and_47_out);
  or or_9 (reg_rt, ADDI, ADDIU, ANDI, ORI, SLTI, LW);
  Comparator #(.width(6)) comparator_59 (.a(MEM_IM[31:26]), .b({6{1'b0}}), .eq(R1_mem));  // open: gt, lt
  Comparator #(.width(6)) comparator_60 (.a(MEM_IM[5:0]), .b(6'b100000), .eq(comparator_60_eq));  // open: gt, lt
  Comparator #(.width(6)) comparator_61 (.a(MEM_IM[5:0]), .b(6'b100001), .eq(comparator_61_eq));  // open: gt, lt
  Comparator #(.width(6)) comparator_62 (.a(MEM_IM[5:0]), .b(6'b100100), .eq(comparator_62_eq));  // open: gt, lt
  Comparator #(.width(6)) comparator_63 (.a(MEM_IM[5:0]), .b({6{1'b0}}), .eq(comparator_63_eq));  // open: gt, lt
  Comparator #(.width(6)) comparator_64 (.a(MEM_IM[5:0]), .b(6'b000100), .eq(comparator_64_eq));  // open: gt, lt
  Comparator #(.width(6)) comparator_65 (.a(MEM_IM[5:0]), .b(6'b000010), .eq(comparator_65_eq));  // open: gt, lt
  Comparator #(.width(6)) comparator_66 (.a(MEM_IM[5:0]), .b(6'b000110), .eq(comparator_66_eq));  // open: gt, lt
  Comparator #(.width(6)) comparator_67 (.a(MEM_IM[5:0]), .b(6'b000011), .eq(comparator_67_eq));  // open: gt, lt
  Comparator #(.width(6)) comparator_68 (.a(MEM_IM[5:0]), .b(6'b100101), .eq(comparator_68_eq));  // open: gt, lt
  Comparator #(.width(6)) comparator_69 (.a(MEM_IM[5:0]), .b(6'b100111), .eq(comparator_69_eq));  // open: gt, lt
  Comparator #(.width(6)) comparator_70 (.a(MEM_IM[5:0]), .b(6'b101010), .eq(comparator_70_eq));  // open: gt, lt
  Comparator #(.width(6)) comparator_71 (.a(MEM_IM[5:0]), .b(6'b101011), .eq(comparator_71_eq));  // open: gt, lt
  Comparator #(.width(6)) comparator_72 (.a(MEM_IM[5:0]), .b(6'b100010), .eq(comparator_72_eq));  // open: gt, lt
  or or_10 (reg_rd_mem, ADD_mem, ADDU_mem, AND_mem, SLL_mem, SLLV_mem, SRL_mem, SRLV_mem, SRA_mem, OR_mem, NOR_mem, SLT_mem, SLTU_mem, SUB_mem);
  and and_49 (ADD_mem, R1_mem, comparator_60_eq);
  and and_50 (ADDU_mem, R1_mem, comparator_61_eq);
  and and_51 (AND_mem, R1_mem, comparator_62_eq);
  and and_52 (SLL_mem, R1_mem, comparator_63_eq);
  and and_53 (SLLV_mem, R1_mem, comparator_64_eq);
  and and_54 (SRL_mem, R1_mem, comparator_65_eq);
  and and_55 (SRLV_mem, R1_mem, comparator_66_eq);
  and and_56 (SRA_mem, R1_mem, comparator_67_eq);
  and and_57 (OR_mem, R1_mem, comparator_68_eq);
  and and_58 (NOR_mem, R1_mem, comparator_69_eq);
  and and_59 (SLT_mem, R1_mem, comparator_70_eq);
  and and_60 (SLTU_mem, R1_mem, comparator_71_eq);
  and and_61 (SUB_mem, R1_mem, comparator_72_eq);
  Multiplexer #(.select(2), .width(5), .enable("false")) multiplexer_2 (
    .in0({5{1'b0}}), .in1(MEM_IM[15:11]), .in2(MEM_IM[20:16]), .in3({5{1'b0}}), .out(regex_mem),
    .sel({reg_rt_mem, reg_rd_mem}));
  Comparator #(.width(6)) comparator_73 (.a(MEM_IM[31:26]), .b(6'b001000), .eq(ADDI_mem));  // open: gt, lt
  Comparator #(.width(6)) comparator_74 (.a(MEM_IM[31:26]), .b(6'b001001), .eq(ADDIU_mem));  // open: gt, lt
  Comparator #(.width(6)) comparator_75 (.a(MEM_IM[31:26]), .b(6'b001100), .eq(ANDI_mem));  // open: gt, lt
  Comparator #(.width(6)) comparator_76 (.a(MEM_IM[31:26]), .b(6'b001101), .eq(ORI_mem));  // open: gt, lt
  Comparator #(.width(6)) comparator_77 (.a(MEM_IM[31:26]), .b(6'b001010), .eq(SLTI_mem));  // open: gt, lt
  Comparator #(.width(6)) comparator_78 (.a(MEM_IM[31:26]), .b(6'b100011), .eq(LW_mem));  // open: gt, lt
  or or_11 (reg_rt_mem, ADDI_mem, ADDIU_mem, ANDI_mem, ORI_mem, SLTI_mem, LW_mem);

  // Other names for the same wires on the sheet: func[5:0] = IM_EX[5:0]; rd[4:0] = IM_EX[15:11];
  //   rt[4:0] = IM_EX[20:16]; operate[5:0] = IM_EX[31:26]; func_id[5:0] = IM_id[5:0]; operate_id[5:0] = IM_id[31:26];
  //   func_mem[5:0] = MEM_IM[5:0]; rd_mem[4:0] = MEM_IM[15:11]; rt_mem[4:0] = MEM_IM[20:16];
  //   operate_mem[5:0] = MEM_IM[31:26]
endmodule

module dbpredictFSM (
  input  [1:0] state_now,
  input  suc_fail,
  output [1:0] state_next
);

  wire [1:0] multiplexer_1_out, multiplexer_2_out, multiplexer_3_out, multiplexer_4_out;

  Multiplexer #(.width(2), .enable("false")) multiplexer_1 (
    .in0(2'b00), .in1(2'b01), .out(multiplexer_1_out), .sel(suc_fail));
  Multiplexer #(.width(2), .enable("false")) multiplexer_2 (
    .in0(2'b00), .in1(2'b11), .out(multiplexer_2_out), .sel(suc_fail));
  Multiplexer #(.width(2), .enable("false")) multiplexer_3 (
    .in0(2'b00), .in1(2'b11), .out(multiplexer_3_out), .sel(suc_fail));
  Multiplexer #(.width(2), .enable("false")) multiplexer_4 (
    .in0(2'b10), .in1(2'b11), .out(multiplexer_4_out), .sel(suc_fail));
  Multiplexer #(.select(2), .width(2), .enable("false")) multiplexer_5 (
    .in0(multiplexer_1_out), .in1(multiplexer_2_out), .in2(multiplexer_3_out), .in3(multiplexer_4_out),
    .out(state_next), .sel(state_now));
endmodule

module BHT_table (
  input  [31:0] PC,
  input  [31:0] newjmpPC,
  input  [31:0] newjmpnextPC,
  input  clk,
  input  rst,
  input  JMP,
  input  CBSUC,
  input  Bs,
  output [31:0] pc_2,
  output [31:0] npc,
  output predict
);

  wire and_1_out, and_2_out, and_3_out, and_4_out, and_5_out, and_6_out, and_7_out, and_8_out, and_10_out,
       bingo, bingonext, comparator_1_eq, comparator_2_eq, comparator_3_eq, comparator_4_eq, comparator_5_gt,
       comparator_6_gt, comparator_7_gt, comparator_8_eq, comparator_9_eq, decoder_1_out0, decoder_1_out1,
       decoder_1_out2, decoder_1_out3, decoder_2_out0, decoder_2_out1, decoder_2_out2, decoder_2_out3,
       decoder_3_out0, decoder_3_out1, decoder_3_out2, decoder_3_out3, decoder_4_out0, decoder_4_out1,
       decoder_4_out2, decoder_4_out3, newjmp, not_1_out, not_2_out, not_3_out, not_4_out, not_5_out,
       or_1_out, or_2_out, or_3_out, or_4_out, or_5_out, or_6_out, or_7_out, or_8_out, or_9_out, or_10_out,
       or_11_out, or_12_out, or_13_out, predictjmp, valid1, valid2, valid3, valid4;
  wire [1:0] change, multiplexer_7_out, multiplexer_8_out, multiplexer_9_out, multiplexer_13_out, next_state,
       priority_encoder_2_out, register_17_q, register_18_q, register_19_q, register_20_q, sel, selnext,
       state, state_q;
  wire [7:0] adder_1_out, adder_2_out, adder_3_out, adder_4_out, multiplexer_1_out, multiplexer_2_out,
       multiplexer_3_out, multiplexer_4_out, multiplexer_5_out, multiplexer_6_out, register_7_q,
       register_8_q, register_9_q, register_10_q;
  wire [31:0] adder_5_out, adder_6_out, multiplexer_12_out, nextPC, nextPC_q, PC_q, register_1_q,
       register_2_q, register_3_q, register_12_q, register_13_q, register_14_q;

  Decoder #(.select(2), .disabled(0)) decoder_1 (
    .out0(decoder_1_out0), .out1(decoder_1_out1), .out2(decoder_1_out2), .out3(decoder_1_out3), .sel(sel),
    .en(bingo));
  Decoder #(.select(2), .disabled(0)) decoder_2 (
    .out0(decoder_2_out0), .out1(decoder_2_out1), .out2(decoder_2_out2), .out3(decoder_2_out3), .sel(change),
    .en(newjmp));
  Decoder #(.select(2), .disabled(0)) decoder_3 (
    .out0(decoder_3_out0), .out1(decoder_3_out1), .out2(decoder_3_out2), .out3(decoder_3_out3), .sel(change),
    .en(newjmp));
  and and_1 (and_1_out, valid1, decoder_1_out0);
  and and_2 (and_2_out, valid2, decoder_1_out1);
  and and_3 (and_3_out, valid3, decoder_1_out2);
  and and_4 (and_4_out, valid4, decoder_1_out3);
  or or_1 (or_1_out, and_1_out, decoder_2_out0);
  or or_2 (or_2_out, and_2_out, decoder_2_out1);
  or or_3 (or_3_out, and_3_out, decoder_2_out2);
  or or_4 (or_4_out, and_4_out, decoder_2_out3);
  Register #(.width(32)) u_PC (.D(newjmpPC), .en(decoder_3_out0), .Q(PC_q), .clk(clk), .clr(rst));
  Register #(.width(32)) register_1 (.D(newjmpPC), .en(decoder_3_out1), .Q(register_1_q), .clk(clk), .clr(rst));
  Register #(.width(32)) register_2 (.D(newjmpPC), .en(decoder_3_out2), .Q(register_2_q), .clk(clk), .clr(rst));
  Register #(.width(32)) register_3 (.D(newjmpPC), .en(decoder_3_out3), .Q(register_3_q), .clk(clk), .clr(rst));
  Comparator #(.width(32), .mode("unsigned")) comparator_1 (.a(PC_q), .b(PC), .eq(comparator_1_eq));  // open: gt, lt
  Comparator #(.width(32), .mode("unsigned")) comparator_2 (
    .a(register_1_q), .b(PC), .eq(comparator_2_eq));  // open: gt, lt
  Comparator #(.width(32), .mode("unsigned")) comparator_3 (
    .a(register_2_q), .b(PC), .eq(comparator_3_eq));  // open: gt, lt
  Comparator #(.width(32), .mode("unsigned")) comparator_4 (
    .a(register_3_q), .b(PC), .eq(comparator_4_eq));  // open: gt, lt
  Adder adder_1 (.a(register_7_q), .b(8'h1), .out(adder_1_out));  // open: cin, cout
  Adder adder_2 (.a(register_8_q), .b(8'h1), .out(adder_2_out));  // open: cin, cout
  Adder adder_3 (.a(register_9_q), .b(8'h1), .out(adder_3_out));  // open: cin, cout
  Adder adder_4 (.a(register_10_q), .b(8'h1), .out(adder_4_out));  // open: cin, cout
  Multiplexer #(.width(8), .enable("false")) multiplexer_1 (
    .in0(adder_1_out), .in1({8{1'b0}}), .out(multiplexer_1_out), .sel(or_1_out));
  Multiplexer #(.width(8), .enable("false")) multiplexer_2 (
    .in0(adder_2_out), .in1({8{1'b0}}), .out(multiplexer_2_out), .sel(or_2_out));
  Multiplexer #(.width(8), .enable("false")) multiplexer_3 (
    .in0(adder_3_out), .in1({8{1'b0}}), .out(multiplexer_3_out), .sel(or_3_out));
  Multiplexer #(.width(8), .enable("false")) multiplexer_4 (
    .in0(adder_4_out), .in1({8{1'b0}}), .out(multiplexer_4_out), .sel(or_4_out));
  or or_5 (or_5_out, newjmp, bingo);
  Register #(.width(1)) valid (.D(1'b1), .en(decoder_3_out0), .Q(valid1), .clk(clk), .clr(rst));
  and and_5 (and_5_out, valid1, comparator_1_eq);
  Register #(.width(1)) register_4 (.D(1'b1), .en(decoder_3_out1), .Q(valid2), .clk(clk), .clr(rst));
  and and_6 (and_6_out, valid2, comparator_2_eq);
  Register #(.width(1)) register_5 (.D(1'b1), .en(decoder_3_out2), .Q(valid3), .clk(clk), .clr(rst));
  and and_7 (and_7_out, valid3, comparator_3_eq);
  Register #(.width(1)) register_6 (.D(1'b1), .en(decoder_3_out3), .Q(valid4), .clk(clk), .clr(rst));
  and and_8 (and_8_out, valid4, comparator_4_eq);
  Register register_7 (.D(multiplexer_1_out), .en(or_5_out), .Q(register_7_q), .clk(clk), .clr(rst));
  Register register_8 (.D(multiplexer_2_out), .en(or_5_out), .Q(register_8_q), .clk(clk), .clr(rst));
  Register register_9 (.D(multiplexer_3_out), .en(or_5_out), .Q(register_9_q), .clk(clk), .clr(rst));
  Register register_10 (.D(multiplexer_4_out), .en(or_5_out), .Q(register_10_q), .clk(clk), .clr(rst));
  // Probe on newjmpnextPC
  Comparator #(.mode("unsigned")) comparator_5 (
    .a(register_7_q), .b(register_8_q), .gt(comparator_5_gt));  // open: eq, lt
  Comparator #(.mode("unsigned")) comparator_6 (
    .a(register_9_q), .b(register_10_q), .gt(comparator_6_gt));  // open: eq, lt
  Priority_Encoder #(.select(2)) priority_encoder_1 (
    .in0(and_5_out), .in1(and_6_out), .in2(and_7_out), .in3(and_8_out), .out(sel), .gs(bingo));  // open: en_out, en_in
  Multiplexer #(.width(8), .enable("false")) multiplexer_5 (
    .in0(register_8_q), .in1(register_7_q), .out(multiplexer_5_out), .sel(comparator_5_gt));
  Multiplexer #(.width(8), .enable("false")) multiplexer_6 (
    .in0(register_10_q), .in1(register_9_q), .out(multiplexer_6_out), .sel(comparator_6_gt));
  Register #(.width(1)) register_11 (.D(bingo), .Q(bingonext), .clk(clk), .clr(rst));  // open: en
  Multiplexer #(.width(2), .enable("false")) multiplexer_7 (
    .in0(2'b01), .in1(2'b00), .out(multiplexer_7_out), .sel(comparator_5_gt));
  Multiplexer #(.width(2), .enable("false")) multiplexer_8 (
    .in0(2'b11), .in1(2'b10), .out(multiplexer_8_out), .sel(comparator_6_gt));
  not not_1 (not_1_out, bingonext);
  or or_6 (or_6_out, JMP, CBSUC);
  Comparator #(.mode("unsigned")) comparator_7 (
    .a(multiplexer_5_out), .b(multiplexer_6_out), .gt(comparator_7_gt));  // open: eq, lt
  Register #(.width(32)) u_nextPC (.D(newjmpnextPC), .en(decoder_3_out0), .Q(nextPC_q), .clk(clk), .clr(rst));
  Register #(.width(32)) register_12 (.D(newjmpnextPC), .en(decoder_3_out1), .Q(register_12_q), .clk(clk), .clr(rst));
  Register #(.width(32)) register_13 (.D(newjmpnextPC), .en(decoder_3_out2), .Q(register_13_q), .clk(clk), .clr(rst));
  Register #(.width(32)) register_14 (.D(newjmpnextPC), .en(decoder_3_out3), .Q(register_14_q), .clk(clk), .clr(rst));
  and and_9 (newjmp, not_1_out, or_6_out);
  Multiplexer #(.width(2), .enable("false")) multiplexer_9 (
    .in0(multiplexer_8_out), .in1(multiplexer_7_out), .out(multiplexer_9_out), .sel(comparator_7_gt));
  not not_2 (not_2_out, valid1);
  not not_3 (not_3_out, valid2);
  not not_4 (not_4_out, valid3);
  not not_5 (not_5_out, valid4);
  or or_7 (or_7_out, ~valid1, ~valid2, ~valid3, ~valid4);  // OR_Gate
  Multiplexer #(.width(2), .enable("false")) multiplexer_10 (
    .in0(multiplexer_9_out), .in1(priority_encoder_2_out), .out(change), .sel(or_7_out));
  Priority_Encoder #(.select(2)) priority_encoder_2 (
    .in0(not_2_out), .in1(not_3_out), .in2(not_4_out), .in3(not_5_out), .out(priority_encoder_2_out));  // open: gs, en_out, en_in
  Multiplexer #(.select(2), .width(32), .enable("false")) multiplexer_11 (
    .in0(nextPC_q), .in1(register_12_q), .in2(register_13_q), .in3(register_14_q), .out(nextPC), .sel(sel));
  Register #(.width(2)) register_15 (.D(sel), .Q(selnext), .clk(clk), .clr(rst));  // open: en
  Adder #(.width(32)) adder_5 (.a(32'h4), .b(PC), .out(adder_5_out));  // open: cin, cout
  Multiplexer #(.width(32), .enable("false")) multiplexer_12 (
    .in0(adder_5_out), .in1(nextPC), .out(multiplexer_12_out), .sel(predictjmp));
  Register #(.width(1)) register_16 (.D(predictjmp), .Q(predict), .clk(clk), .clr(rst));  // open: en
  Decoder #(.select(2), .disabled(0)) decoder_4 (
    .out0(decoder_4_out0), .out1(decoder_4_out1), .out2(decoder_4_out2), .out3(decoder_4_out3),
    .sel(selnext), .en(bingonext));
  Adder #(.width(32)) adder_6 (.a(32'h4), .b(newjmpPC), .out(adder_6_out));  // open: cin, cout
  and and_10 (and_10_out, ~CBSUC, Bs);  // AND_Gate
  Multiplexer #(.width(2), .enable("false")) multiplexer_13 (
    .in0(2'b00), .in1(next_state), .out(multiplexer_13_out), .sel(bingonext));
  or or_8 (or_8_out, decoder_3_out0, decoder_4_out0);
  or or_9 (or_9_out, decoder_3_out1, decoder_4_out1);
  or or_10 (or_10_out, decoder_4_out2, decoder_3_out2);
  or or_11 (or_11_out, decoder_4_out3, decoder_3_out3);
  Comparator #(.width(2)) comparator_8 (.a(2'b10), .b(state), .eq(comparator_8_eq));  // open: gt, lt
  Comparator #(.width(2)) comparator_9 (.a(state), .b(2'b11), .eq(comparator_9_eq));  // open: gt, lt
  Multiplexer #(.width(32), .enable("false")) multiplexer_14 (
    .in0(multiplexer_12_out), .in1(adder_6_out), .out(npc), .sel(and_10_out));
  Register #(.width(2)) u_state (.D(multiplexer_13_out), .en(or_8_out), .Q(state_q), .clk(clk), .clr(rst));
  Register #(.width(2)) register_17 (.D(multiplexer_13_out), .en(or_9_out), .Q(register_17_q), .clk(clk), .clr(rst));
  Register #(.width(2)) register_18 (.D(multiplexer_13_out), .en(or_10_out), .Q(register_18_q), .clk(clk), .clr(rst));
  Register #(.width(2)) register_19 (.D(multiplexer_13_out), .en(or_11_out), .Q(register_19_q), .clk(clk), .clr(rst));
  or or_12 (or_12_out, comparator_8_eq, comparator_9_eq);
  Multiplexer #(.select(2), .width(2), .disabled(0)) multiplexer_15 (
    .in0(state_q), .in1(register_17_q), .in2(register_18_q), .in3(register_19_q), .out(state), .sel(sel),
    .en(bingo));
  Register #(.width(2)) register_20 (.D(state), .Q(register_20_q), .clk(clk), .clr(rst));  // open: en
  and and_11 (predictjmp, or_12_out, bingo);
  dbpredictFSM dbpredictfsm_1 (.state_now(register_20_q), .suc_fail(or_13_out), .state_next(next_state));
  or or_13 (or_13_out, JMP, CBSUC);

  assign pc_2 = PC;
endmodule
